// Logisim project ayesha and abdullah final interface.circ as structural Verilog
// NOT
module NOT_Gate (
  input  in_1,
  output out_2
);

  Pull_Resistor pull_resistor_1 (.node(out_2));
  Transistor transistor_1 (.in(1'b1), .out(out_2), .gate(in_1));
endmodule

module BUFFER_Gate (
  input  in_1,
  input  in_2,
  output out_3
);

  Transistor #(.\type ("n")) transistor_1 (.in(in_2), .out(out_3), .gate(in_1));
  Pull_Resistor pull_resistor_1 (.node(out_3));
endmodule

// AND
module AND_Gate (
  input  in_1,
  input  in_2,
  output out_3
);

  wire transistor_1_out;

  Transistor #(.\type ("n")) transistor_1 (.in(1'b1), .out(transistor_1_out), .gate(in_1));
  Pull_Resistor pull_resistor_1 (.node(transistor_1_out));
  Pull_Resistor pull_resistor_2 (.node(out_3));
  Transistor #(.\type ("n")) transistor_2 (.in(transistor_1_out), .out(out_3), .gate(in_2));
endmodule

// AND - 3
module AND_Gate___3 (
  input  in_1,
  input  in_2,
  input  in_3,
  output out_4
);

  wire transistor_1_out, transistor_2_out;

  Transistor #(.\type ("n")) transistor_1 (.in(1'b1), .out(transistor_1_out), .gate(in_1));
  Transistor #(.\type ("n")) transistor_2 (.in(transistor_1_out), .out(transistor_2_out), .gate(in_2));
  Pull_Resistor pull_resistor_1 (.node(transistor_1_out));
  Pull_Resistor pull_resistor_2 (.node(transistor_2_out));
  Transistor #(.\type ("n")) transistor_3 (.in(transistor_2_out), .out(out_4), .gate(in_3));
  Pull_Resistor pull_resistor_3 (.node(out_4));
endmodule

// AND
module AND_Gate___4 (
  input  in_1,
  input  in_2,
  input  in_3,
  input  in_4,
  output out_5
);

  wire transistor_1_out, transistor_2_out, transistor_3_out;

  Transistor #(.\type ("n")) transistor_1 (.in(1'b1), .out(transistor_1_out), .gate(in_1));
  Transistor #(.\type ("n")) transistor_2 (.in(transistor_1_out), .out(transistor_2_out), .gate(in_2));
  Pull_Resistor pull_resistor_1 (.node(transistor_1_out));
  Pull_Resistor pull_resistor_2 (.node(transistor_2_out));
  Transistor #(.\type ("n")) transistor_3 (.in(transistor_2_out), .out(transistor_3_out), .gate(in_3));
  Pull_Resistor pull_resistor_3 (.node(transistor_3_out));
  Transistor #(.\type ("n")) transistor_4 (.in(transistor_3_out), .out(out_5), .gate(in_4));
  Pull_Resistor pull_resistor_4 (.node(out_5));
endmodule

// AND
module AND_Gate___5 (
  input  in_1,
  input  in_2,
  input  in_3,
  input  in_4,
  input  in_5,
  output out_6
);

  wire transistor_1_out, transistor_2_out, transistor_3_out, transistor_5_out;

  Transistor #(.\type ("n")) transistor_1 (.in(1'b1), .out(transistor_1_out), .gate(in_1));
  Transistor #(.\type ("n")) transistor_2 (.in(transistor_1_out), .out(transistor_2_out), .gate(in_2));
  Pull_Resistor pull_resistor_1 (.node(transistor_1_out));
  Pull_Resistor pull_resistor_2 (.node(transistor_2_out));
  Transistor #(.\type ("n")) transistor_3 (.in(transistor_2_out), .out(transistor_3_out), .gate(in_3));
  Pull_Resistor pull_resistor_3 (.node(transistor_3_out));
  Transistor #(.\type ("n")) transistor_4 (.in(transistor_5_out), .out(out_6), .gate(in_5));
  Transistor #(.\type ("n")) transistor_5 (.in(transistor_3_out), .out(transistor_5_out), .gate(in_4));
  Pull_Resistor pull_resistor_4 (.node(transistor_5_out));
  Pull_Resistor pull_resistor_5 (.node(out_6));
endmodule

// AND
module AND_Gate___9 (
  input  in_1,
  input  in_2,
  input  in_3,
  input  in_4,
  input  in_5,
  input  in_6,
  input  in_7,
  input  in_8,
  input  in_9,
  output out_10
);

  wire pull_resistor_1_node, pull_resistor_4_node, pull_resistor_5_node, pull_resistor_6_node,
       pull_resistor_7_node, transistor_2_out, transistor_3_out, transistor_8_out;

  Pull_Resistor pull_resistor_1 (.node(pull_resistor_1_node));
  Transistor #(.\type ("n")) transistor_1 (.in(1'b1), .out(pull_resistor_1_node), .gate(in_1));
  Transistor #(.\type ("n")) transistor_2 (.in(pull_resistor_1_node), .out(transistor_2_out), .gate(in_2));
  Pull_Resistor pull_resistor_2 (.node(transistor_2_out));
  Transistor #(.\type ("n")) transistor_3 (.in(transistor_2_out), .out(transistor_3_out), .gate(in_3));
  Pull_Resistor pull_resistor_3 (.node(transistor_3_out));
  Pull_Resistor pull_resistor_4 (.node(pull_resistor_4_node));
  Transistor #(.\type ("n")) transistor_4 (.in(transistor_3_out), .out(pull_resistor_4_node), .gate(in_4));
  Pull_Resistor pull_resistor_5 (.node(pull_resistor_5_node));
  Transistor #(.\type ("n")) transistor_5 (.in(pull_resistor_4_node), .out(pull_resistor_5_node), .gate(in_5));
  Pull_Resistor pull_resistor_6 (.node(pull_resistor_6_node));
  Transistor #(.\type ("n")) transistor_6 (.in(pull_resistor_5_node), .out(pull_resistor_6_node), .gate(in_6));
  Pull_Resistor pull_resistor_7 (.node(pull_resistor_7_node));
  Transistor #(.\type ("n")) transistor_7 (.in(pull_resistor_6_node), .out(pull_resistor_7_node), .gate(in_7));
  Transistor #(.\type ("n")) transistor_8 (.in(pull_resistor_7_node), .out(transistor_8_out), .gate(in_8));
  Pull_Resistor pull_resistor_8 (.node(transistor_8_out));
  Pull_Resistor pull_resistor_9 (.node(out_10));
  Transistor #(.\type ("n")) transistor_9 (.in(transistor_8_out), .out(out_10), .gate(in_9));
endmodule

// OR
module OR_Gate (
  input  in_1,
  input  in_2,
  output out_3
);

  Transistor #(.\type ("n")) transistor_1 (.in(1'b1), .out(out_3), .gate(in_1));
  Transistor #(.\type ("n")) transistor_2 (.in(1'b1), .out(out_3), .gate(in_2));
  Pull_Resistor pull_resistor_1 (.node(out_3));
endmodule

// OR
module OR_Gate___3 (
  input  in_1,
  input  in_2,
  input  in_3,
  output out_4
);

  Transistor #(.\type ("n")) transistor_1 (.in(1'b1), .out(out_4), .gate(in_1));
  Transistor #(.\type ("n")) transistor_2 (.in(1'b1), .out(out_4), .gate(in_2));
  Pull_Resistor pull_resistor_1 (.node(out_4));
  Transistor #(.\type ("n")) transistor_3 (.in(1'b1), .out(out_4), .gate(in_3));
endmodule

// OR
module OR_Gate___5 (
  input  in_1,
  input  in_2,
  input  in_3,
  input  in_4,
  input  in_5,
  output out_6
);

  Transistor #(.\type ("n")) transistor_1 (.in(1'b1), .out(out_6), .gate(in_1));
  Transistor #(.\type ("n")) transistor_2 (.in(1'b1), .out(out_6), .gate(in_2));
  Transistor #(.\type ("n")) transistor_3 (.in(1'b1), .out(out_6), .gate(in_3));
  Transistor #(.\type ("n")) transistor_4 (.in(1'b1), .out(out_6), .gate(in_4));
  Transistor #(.\type ("n")) transistor_5 (.in(1'b1), .out(out_6), .gate(in_5));
  Pull_Resistor pull_resistor_1 (.node(out_6));
endmodule

// OR
module OR_Gate___7 (
  input  in_1,
  input  in_2,
  input  in_3,
  input  in_4,
  input  in_5,
  input  in_6,
  input  in_7,
  output out_8
);

  Transistor #(.\type ("n")) transistor_1 (.in(1'b1), .out(out_8), .gate(in_1));
  Transistor #(.\type ("n")) transistor_2 (.in(1'b1), .out(out_8), .gate(in_2));
  Transistor #(.\type ("n")) transistor_3 (.in(1'b1), .out(out_8), .gate(in_3));
  Transistor #(.\type ("n")) transistor_4 (.in(1'b1), .out(out_8), .gate(in_4));
  Transistor #(.\type ("n")) transistor_5 (.in(1'b1), .out(out_8), .gate(in_5));
  Transistor #(.\type ("n")) transistor_6 (.in(1'b1), .out(out_8), .gate(in_6));
  Transistor #(.\type ("n")) transistor_7 (.in(1'b1), .out(out_8), .gate(in_7));
  Pull_Resistor pull_resistor_1 (.node(out_8));
endmodule

module OR_Gate___8 (
  input  in_1,
  input  in_2,
  input  in_3,
  input  in_4,
  input  in_5,
  input  in_6,
  input  in_7,
  input  in_8,
  output out_9
);

  Transistor #(.\type ("n")) transistor_1 (.in(1'b1), .out(out_9), .gate(in_1));
  Transistor #(.\type ("n")) transistor_2 (.in(1'b1), .out(out_9), .gate(in_2));
  Transistor #(.\type ("n")) transistor_3 (.in(1'b1), .out(out_9), .gate(in_3));
  Transistor #(.\type ("n")) transistor_4 (.in(1'b1), .out(out_9), .gate(in_4));
  Transistor #(.\type ("n")) transistor_5 (.in(1'b1), .out(out_9), .gate(in_5));
  Transistor #(.\type ("n")) transistor_6 (.in(1'b1), .out(out_9), .gate(in_6));
  Transistor #(.\type ("n")) transistor_7 (.in(1'b1), .out(out_9), .gate(in_7));
  Transistor #(.\type ("n")) transistor_8 (.in(1'b1), .out(out_9), .gate(in_8));
  Pull_Resistor pull_resistor_1 (.node(out_9));
endmodule

// NAND
module NAND_Gate (
  input  in_1,
  input  in_2,
  output out_3
);

  Transistor transistor_1 (.in(1'b1), .out(out_3), .gate(in_1));
  Pull_Resistor pull_resistor_1 (.node(out_3));
  Transistor transistor_2 (.in(1'b1), .out(out_3), .gate(in_2));
endmodule

// NOR
module NOR_Gate (
  input  in_1,
  input  in_2,
  output out_3
);

  wire transistor_1_out;

  Transistor transistor_1 (.in(1'b1), .out(transistor_1_out), .gate(in_1));
  Pull_Resistor pull_resistor_1 (.node(transistor_1_out));
  Transistor transistor_2 (.in(transistor_1_out), .out(out_3), .gate(in_2));
  Pull_Resistor pull_resistor_2 (.node(out_3));
endmodule

// XOR
module XOR_Gate (
  input  in_1,
  input  in_2,
  output out_3
);

  wire pull_resistor_2_node, pull_resistor_3_node, transistor_1_out;

  Transistor transistor_1 (.in(1'b1), .out(transistor_1_out), .gate(in_1));
  Pull_Resistor pull_resistor_1 (.node(transistor_1_out));
  Transistor transistor_2 (.in(1'b1), .out(transistor_1_out), .gate(in_2));
  Pull_Resistor pull_resistor_2 (.node(pull_resistor_2_node));
  Transistor transistor_3 (.in(1'b1), .out(pull_resistor_2_node), .gate(in_1));
  Transistor transistor_4 (.in(1'b1), .out(pull_resistor_2_node), .gate(transistor_1_out));
  Pull_Resistor pull_resistor_3 (.node(pull_resistor_3_node));
  Transistor transistor_5 (.in(1'b1), .out(pull_resistor_3_node), .gate(in_2));
  Transistor transistor_6 (.in(1'b1), .out(pull_resistor_3_node), .gate(transistor_1_out));
  Transistor transistor_7 (.in(1'b1), .out(out_3), .gate(pull_resistor_2_node));
  Transistor transistor_8 (.in(1'b1), .out(out_3), .gate(pull_resistor_3_node));
  Pull_Resistor pull_resistor_4 (.node(out_3));
endmodule

// MAJ
module MAJORITY_Gate (
  input  A,
  input  B,
  input  C,
  output X
);

  wire nand_1_out_3, nand_2_out_3, nand_3_out_3, nand_4_out_3, nand_5_out_3;

  NAND_Gate nand_1 (.out_3(nand_1_out_3), .in_1(A), .in_2(B));
  NAND_Gate nand_2 (.out_3(nand_2_out_3), .in_1(A), .in_2(C));
  NAND_Gate nand_3 (.out_3(nand_3_out_3), .in_1(B), .in_2(C));
  NAND_Gate nand_4 (.out_3(nand_4_out_3), .in_1(nand_1_out_3), .in_2(nand_2_out_3));
  NAND_Gate nand_5 (.out_3(nand_5_out_3), .in_1(nand_4_out_3), .in_2(nand_4_out_3));
  NAND_Gate nand_6 (.out_3(X), .in_1(nand_5_out_3), .in_2(nand_3_out_3));
endmodule

module circuit (
);


  // Notes on the sheet:
  //   couldnt have asked for a better teammate
endmodule

module Half_Adder (
  input  A,
  input  B,
  output Sum,
  output Carry
);

  XOR_Gate xor_1 (.in_1(A), .in_2(B), .out_3(Sum));
  AND_Gate and_1 (.out_3(Carry), .in_1(B), .in_2(A));
endmodule

module Full_Adder (
  input  A,
  input  B,
  input  Carry_in,
  output Sum,
  output Carry_out
);

  wire and_1_out_3, and_2_out_3, xor_1_out_3;

  XOR_Gate xor_1 (.in_1(A), .in_2(B), .out_3(xor_1_out_3));
  AND_Gate and_1 (.out_3(and_1_out_3), .in_1(B), .in_2(A));
  AND_Gate and_2 (.out_3(and_2_out_3), .in_1(xor_1_out_3), .in_2(Carry_in));
  XOR_Gate xor_2 (.in_1(xor_1_out_3), .in_2(Carry_in), .out_3(Sum));
  OR_Gate or_1 (.out_3(Carry_out), .in_1(and_1_out_3), .in_2(and_2_out_3));
endmodule

// MX Adder
module Full_Adder__MAJ__XOR (
  input  A,
  input  B,
  input  C,
  output Sum,
  output Carry
);

  wire xor_1_out_3;

  XOR_Gate xor_1 (.in_1(A), .in_2(B), .out_3(xor_1_out_3));
  MAJORITY_Gate majority_1 (.X(Carry), .A(A), .B(B), .C(C));
  XOR_Gate xor_2 (.in_1(xor_1_out_3), .in_2(C), .out_3(Sum));
endmodule

// Adder
module _8_Bit_Adder (
  input  in_1,
  input  in_2,
  input  in_3,
  input  in_4,
  input  in_5,
  input  in_6,
  input  in_7,
  input  Byte_A,
  input  in_9,
  input  in_10,
  input  in_11,
  input  in_12,
  input  in_13,
  input  in_14,
  input  in_15,
  input  Byte_B,
  output Carry_Out,
  output out_18,
  output out_19,
  output out_20,
  output out_21,
  output out_22,
  output out_23,
  output out_24,
  output out_25
);

  wire full_adder_maj_xor_2_carry, full_adder_maj_xor_3_carry, full_adder_maj_xor_4_carry,
       full_adder_maj_xor_5_carry, full_adder_maj_xor_6_carry, full_adder_maj_xor_7_carry,
       full_adder_maj_xor_8_carry;

  Full_Adder__MAJ__XOR full_adder_maj_xor_1 (
    .A(in_1), .B(in_9), .C(full_adder_maj_xor_2_carry), .Sum(out_18), .Carry(Carry_Out));
  Full_Adder__MAJ__XOR full_adder_maj_xor_2 (
    .A(in_2), .B(in_10), .C(full_adder_maj_xor_3_carry), .Sum(out_19), .Carry(full_adder_maj_xor_2_carry));
  Full_Adder__MAJ__XOR full_adder_maj_xor_3 (
    .A(in_3), .B(in_11), .C(full_adder_maj_xor_4_carry), .Sum(out_20), .Carry(full_adder_maj_xor_3_carry));
  Full_Adder__MAJ__XOR full_adder_maj_xor_4 (
    .A(in_4), .B(in_12), .C(full_adder_maj_xor_5_carry), .Sum(out_21), .Carry(full_adder_maj_xor_4_carry));
  Full_Adder__MAJ__XOR full_adder_maj_xor_5 (
    .A(in_5), .B(in_13), .C(full_adder_maj_xor_6_carry), .Sum(out_22), .Carry(full_adder_maj_xor_5_carry));
  Full_Adder__MAJ__XOR full_adder_maj_xor_6 (
    .A(in_6), .B(in_14), .C(full_adder_maj_xor_7_carry), .Sum(out_23), .Carry(full_adder_maj_xor_6_carry));
  Full_Adder__MAJ__XOR full_adder_maj_xor_7 (
    .A(in_7), .B(in_15), .C(full_adder_maj_xor_8_carry), .Sum(out_24), .Carry(full_adder_maj_xor_7_carry));
  Full_Adder__MAJ__XOR full_adder_maj_xor_8 (
    .A(Byte_A), .B(Byte_B), .C(1'b0), .Sum(out_25), .Carry(full_adder_maj_xor_8_carry));

  // Notes on the sheet:
  //   Sum Byte
endmodule

// XOR
module _8_Bit_XOR (
  input  in_1,
  input  in_2,
  input  in_3,
  input  in_4,
  input  in_5,
  input  in_6,
  input  in_7,
  input  Byte_A,
  input  in_9,
  input  in_10,
  input  in_11,
  input  in_12,
  input  in_13,
  input  in_14,
  input  in_15,
  input  Byte_B,
  output out_17,
  output out_18,
  output out_19,
  output out_20,
  output out_21,
  output out_22,
  output out_23,
  output out_24
);

  XOR_Gate xor_1 (.in_1(in_1), .in_2(in_9), .out_3(out_17));
  XOR_Gate xor_2 (.in_1(in_2), .in_2(in_10), .out_3(out_18));
  XOR_Gate xor_3 (.in_1(in_3), .in_2(in_11), .out_3(out_19));
  XOR_Gate xor_4 (.in_1(in_4), .in_2(in_12), .out_3(out_20));
  XOR_Gate xor_5 (.in_1(in_5), .in_2(in_13), .out_3(out_21));
  XOR_Gate xor_6 (.in_1(in_6), .in_2(in_14), .out_3(out_22));
  XOR_Gate xor_7 (.in_1(in_7), .in_2(in_15), .out_3(out_23));
  XOR_Gate xor_8 (.in_1(Byte_A), .in_2(Byte_B), .out_3(out_24));

  // Notes on the sheet:
  //   XOR Byte
endmodule

// AND
module _8_Bit_AND (
  input  in_1,
  input  in_2,
  input  in_3,
  input  in_4,
  input  in_5,
  input  in_6,
  input  in_7,
  input  Byte_A,
  input  in_9,
  input  in_10,
  input  in_11,
  input  in_12,
  input  in_13,
  input  in_14,
  input  in_15,
  input  Byte_B,
  output out_17,
  output out_18,
  output out_19,
  output out_20,
  output out_21,
  output out_22,
  output out_23,
  output out_24
);

  AND_Gate and_1 (.out_3(out_17), .in_1(in_9), .in_2(in_1));
  AND_Gate and_2 (.out_3(out_18), .in_1(in_10), .in_2(in_2));
  AND_Gate and_3 (.out_3(out_19), .in_1(in_11), .in_2(in_3));
  AND_Gate and_4 (.out_3(out_20), .in_1(in_12), .in_2(in_4));
  AND_Gate and_5 (.out_3(out_21), .in_1(in_13), .in_2(in_5));
  AND_Gate and_6 (.out_3(out_22), .in_1(in_14), .in_2(in_6));
  AND_Gate and_7 (.out_3(out_23), .in_1(in_15), .in_2(in_7));
  AND_Gate and_8 (.out_3(out_24), .in_1(Byte_B), .in_2(Byte_A));

  // Notes on the sheet:
  //   AND Byte
endmodule

// Adder / Subtractor
module _8_Bit_Adder__Subtractor (
  input  in_1,
  input  in_2,
  input  in_3,
  input  in_4,
  input  in_5,
  input  in_6,
  input  in_7,
  input  Byte_A,
  input  in_9,
  input  in_10,
  input  in_11,
  input  in_12,
  input  in_13,
  input  in_14,
  input  in_15,
  input  in_16,
  input  _0___Adder,
  output out_18,
  output out_19,
  output out_20,
  output out_21,
  output out_22,
  output out_23,
  output out_24,
  output out_25,
  output out_26
);

  wire full_adder_maj_xor_2_carry, full_adder_maj_xor_3_carry, full_adder_maj_xor_4_carry,
       full_adder_maj_xor_5_carry, full_adder_maj_xor_6_carry, full_adder_maj_xor_7_carry,
       full_adder_maj_xor_8_carry, xor_1_out_3, xor_2_out_3, xor_3_out_3, xor_4_out_3, xor_5_out_3,
       xor_6_out_3, xor_7_out_3, xor_8_out_3;

  XOR_Gate xor_1 (.in_1(_0___Adder), .in_2(in_9), .out_3(xor_1_out_3));
  XOR_Gate xor_2 (.in_1(_0___Adder), .in_2(in_10), .out_3(xor_2_out_3));
  Full_Adder__MAJ__XOR full_adder_maj_xor_1 (
    .A(in_1), .B(xor_1_out_3), .C(full_adder_maj_xor_2_carry), .Sum(out_19), .Carry(out_18));
  Full_Adder__MAJ__XOR full_adder_maj_xor_2 (
    .A(in_2), .B(xor_2_out_3), .C(full_adder_maj_xor_3_carry), .Sum(out_20),
    .Carry(full_adder_maj_xor_2_carry));
  XOR_Gate xor_3 (.in_1(_0___Adder), .in_2(in_11), .out_3(xor_3_out_3));
  Full_Adder__MAJ__XOR full_adder_maj_xor_3 (
    .A(in_3), .B(xor_3_out_3), .C(full_adder_maj_xor_4_carry), .Sum(out_21),
    .Carry(full_adder_maj_xor_3_carry));
  XOR_Gate xor_4 (.in_1(_0___Adder), .in_2(in_12), .out_3(xor_4_out_3));
  Full_Adder__MAJ__XOR full_adder_maj_xor_4 (
    .A(in_4), .B(xor_4_out_3), .C(full_adder_maj_xor_5_carry), .Sum(out_22),
    .Carry(full_adder_maj_xor_4_carry));
  XOR_Gate xor_5 (.in_1(_0___Adder), .in_2(in_13), .out_3(xor_5_out_3));
  Full_Adder__MAJ__XOR full_adder_maj_xor_5 (
    .A(in_5), .B(xor_5_out_3), .C(full_adder_maj_xor_6_carry), .Sum(out_23),
    .Carry(full_adder_maj_xor_5_carry));
  XOR_Gate xor_6 (.in_1(_0___Adder), .in_2(in_14), .out_3(xor_6_out_3));
  Full_Adder__MAJ__XOR full_adder_maj_xor_6 (
    .A(in_6), .B(xor_6_out_3), .C(full_adder_maj_xor_7_carry), .Sum(out_24),
    .Carry(full_adder_maj_xor_6_carry));
  XOR_Gate xor_7 (.in_1(_0___Adder), .in_2(in_15), .out_3(xor_7_out_3));
  Full_Adder__MAJ__XOR full_adder_maj_xor_7 (
    .A(in_7), .B(xor_7_out_3), .C(full_adder_maj_xor_8_carry), .Sum(out_25),
    .Carry(full_adder_maj_xor_7_carry));
  XOR_Gate xor_8 (.in_1(_0___Adder), .in_2(in_16), .out_3(xor_8_out_3));
  Full_Adder__MAJ__XOR full_adder_maj_xor_8 (
    .A(Byte_A), .B(xor_8_out_3), .C(_0___Adder), .Sum(out_26), .Carry(full_adder_maj_xor_8_carry));

  // Notes on the sheet:
  //   Byte B
  //   1 - Subtractor
endmodule

module Decoder_2_4 (
  input  A,
  input  B,
  output out_3,
  output out_4,
  output out_5,
  output out_6
);

  wire not_1_out_2, not_2_out_2;

  NOT_Gate not_1 (.out_2(not_1_out_2), .in_1(A));
  NOT_Gate not_2 (.out_2(not_2_out_2), .in_1(B));
  AND_Gate and_1 (.out_3(out_3), .in_1(not_2_out_2), .in_2(not_1_out_2));
  AND_Gate and_2 (.out_3(out_4), .in_1(B), .in_2(not_1_out_2));
  AND_Gate and_3 (.out_3(out_5), .in_1(not_2_out_2), .in_2(A));
  AND_Gate and_4 (.out_3(out_6), .in_1(A), .in_2(B));

  // Notes on the sheet:
  //   A'
  //   B'
endmodule

// Decoder
module Decoder_3_8 (
  input  A,
  input  B,
  input  C,
  output out_4,
  output out_5,
  output out_6,
  output out_7,
  output out_8,
  output out_9,
  output out_10,
  output out_11
);

  wire not_1_out_2, not_2_out_2, not_3_out_2;

  NOT_Gate not_1 (.out_2(not_1_out_2), .in_1(B));
  NOT_Gate not_2 (.out_2(not_2_out_2), .in_1(A));
  NOT_Gate not_3 (.out_2(not_3_out_2), .in_1(C));
  AND_Gate___3 and_3_1 (.in_1(not_2_out_2), .in_2(not_1_out_2), .in_3(not_3_out_2), .out_4(out_4));
  AND_Gate___3 and_3_2 (.in_1(not_2_out_2), .in_2(not_1_out_2), .in_3(C), .out_4(out_5));
  AND_Gate___3 and_3_3 (.in_1(not_2_out_2), .in_2(B), .in_3(not_3_out_2), .out_4(out_6));
  AND_Gate___3 and_3_4 (.in_1(not_2_out_2), .in_2(B), .in_3(C), .out_4(out_7));
  AND_Gate___3 and_3_5 (.in_1(A), .in_2(not_1_out_2), .in_3(not_3_out_2), .out_4(out_8));
  AND_Gate___3 and_3_6 (.in_1(A), .in_2(not_1_out_2), .in_3(C), .out_4(out_9));
  AND_Gate___3 and_3_7 (.in_1(A), .in_2(B), .in_3(not_3_out_2), .out_4(out_10));
  AND_Gate___3 and_3_8 (.in_1(A), .in_2(B), .in_3(C), .out_4(out_11));

  // Notes on the sheet:
  //   A'
  //   B'
  //   C'
endmodule

module Decoder1_2 (
  input  in_1,
  output out_2,
  output out_3
);

  NOT_Gate not_1 (.out_2(out_2), .in_1(in_1));

  assign out_3 = in_1;
endmodule

module Demultiplexer_1_4 (
  input  A,
  input  B,
  input  Data,
  output out_4,
  output out_5,
  output out_6,
  output out_7
);

  wire not_1_out_2, not_2_out_2;

  NOT_Gate not_1 (.out_2(not_1_out_2), .in_1(A));
  NOT_Gate not_2 (.out_2(not_2_out_2), .in_1(B));
  AND_Gate___3 and_3_1 (.in_1(Data), .in_2(not_1_out_2), .in_3(not_2_out_2), .out_4(out_4));
  AND_Gate___3 and_3_2 (.in_1(Data), .in_2(not_1_out_2), .in_3(B), .out_4(out_5));
  AND_Gate___3 and_3_3 (.in_1(Data), .in_2(A), .in_3(not_2_out_2), .out_4(out_6));
  AND_Gate___3 and_3_4 (.in_1(Data), .in_2(A), .in_3(B), .out_4(out_7));

  // Notes on the sheet:
  //   A'
  //   B'
endmodule

// Demux
module Demultiplexer_3_8 (
  input  A,
  input  B,
  input  C,
  input  Data,
  output out_5,
  output out_6,
  output out_7,
  output out_8,
  output out_9,
  output out_10,
  output out_11,
  output out_12
);

  wire and_3_1_out_4, and_3_2_out_4, and_3_3_out_4, and_3_4_out_4, and_3_5_out_4, and_3_6_out_4,
       and_3_7_out_4, and_3_8_out_4, not_1_out_2, not_2_out_2, not_3_out_2;

  NOT_Gate not_1 (.out_2(not_1_out_2), .in_1(B));
  NOT_Gate not_2 (.out_2(not_2_out_2), .in_1(A));
  NOT_Gate not_3 (.out_2(not_3_out_2), .in_1(C));
  AND_Gate___3 and_3_1 (.in_1(not_2_out_2), .in_2(not_1_out_2), .in_3(not_3_out_2), .out_4(and_3_1_out_4));
  AND_Gate___3 and_3_2 (.in_1(not_2_out_2), .in_2(not_1_out_2), .in_3(C), .out_4(and_3_2_out_4));
  AND_Gate___3 and_3_3 (.in_1(not_2_out_2), .in_2(B), .in_3(not_3_out_2), .out_4(and_3_3_out_4));
  AND_Gate___3 and_3_4 (.in_1(not_2_out_2), .in_2(B), .in_3(C), .out_4(and_3_4_out_4));
  AND_Gate___3 and_3_5 (.in_1(A), .in_2(not_1_out_2), .in_3(not_3_out_2), .out_4(and_3_5_out_4));
  AND_Gate___3 and_3_6 (.in_1(A), .in_2(not_1_out_2), .in_3(C), .out_4(and_3_6_out_4));
  AND_Gate___3 and_3_7 (.in_1(A), .in_2(B), .in_3(not_3_out_2), .out_4(and_3_7_out_4));
  AND_Gate___3 and_3_8 (.in_1(A), .in_2(B), .in_3(C), .out_4(and_3_8_out_4));
  AND_Gate and_1 (.out_3(out_5), .in_1(Data), .in_2(and_3_1_out_4));
  AND_Gate and_2 (.out_3(out_6), .in_1(Data), .in_2(and_3_2_out_4));
  AND_Gate and_3 (.out_3(out_7), .in_1(Data), .in_2(and_3_3_out_4));
  AND_Gate and_4 (.out_3(out_8), .in_1(Data), .in_2(and_3_4_out_4));
  AND_Gate and_5 (.out_3(out_9), .in_1(Data), .in_2(and_3_5_out_4));
  AND_Gate and_6 (.out_3(out_10), .in_1(Data), .in_2(and_3_6_out_4));
  AND_Gate and_7 (.out_3(out_11), .in_1(Data), .in_2(and_3_7_out_4));
  AND_Gate and_8 (.out_3(out_12), .in_1(Data), .in_2(and_3_8_out_4));

  // Notes on the sheet:
  //   A'
  //   B'
  //   C'
endmodule

// D/DX 2-4
module Decoder__Demultiplexer_2_4 (
  input  A,
  input  B,
  input  Data,
  output out_4,
  output out_5,
  output out_6,
  output out_7,
  output out_8,
  output out_9,
  output out_10,
  output out_11
);

  wire not_1_out_2, not_2_out_2;

  NOT_Gate not_1 (.out_2(not_1_out_2), .in_1(A));
  NOT_Gate not_2 (.out_2(not_2_out_2), .in_1(B));
  AND_Gate and_1 (.out_3(out_4), .in_1(not_2_out_2), .in_2(not_1_out_2));
  AND_Gate and_2 (.out_3(out_6), .in_1(B), .in_2(not_1_out_2));
  AND_Gate and_3 (.out_3(out_8), .in_1(not_2_out_2), .in_2(A));
  AND_Gate and_4 (.out_3(out_10), .in_1(B), .in_2(A));
  AND_Gate and_5 (.out_3(out_5), .in_1(Data), .in_2(out_4));
  AND_Gate and_6 (.out_3(out_7), .in_1(Data), .in_2(out_6));
  AND_Gate and_7 (.out_3(out_9), .in_1(Data), .in_2(out_8));
  AND_Gate and_8 (.out_3(out_11), .in_1(Data), .in_2(out_10));

  // Notes on the sheet:
  //   A'
  //   B'
endmodule

// D/DX 3-8
module Decoder__Demultiplexer_3_8 (
  input  A,
  input  B,
  input  C,
  input  Data,
  output out_5,
  output out_6,
  output out_7,
  output out_8,
  output out_9,
  output out_10,
  output out_11,
  output out_12,
  output out_13,
  output out_14,
  output out_15,
  output out_16,
  output out_17,
  output out_18,
  output out_19,
  output out_20
);

  wire not_1_out_2, not_2_out_2, not_3_out_2;

  NOT_Gate not_1 (.out_2(not_1_out_2), .in_1(B));
  NOT_Gate not_2 (.out_2(not_2_out_2), .in_1(A));
  NOT_Gate not_3 (.out_2(not_3_out_2), .in_1(C));
  AND_Gate___3 and_3_1 (.in_1(not_2_out_2), .in_2(not_1_out_2), .in_3(not_3_out_2), .out_4(out_5));
  AND_Gate___3 and_3_2 (.in_1(not_2_out_2), .in_2(not_1_out_2), .in_3(C), .out_4(out_7));
  AND_Gate___3 and_3_3 (.in_1(not_2_out_2), .in_2(B), .in_3(not_3_out_2), .out_4(out_9));
  AND_Gate___3 and_3_4 (.in_1(not_2_out_2), .in_2(B), .in_3(C), .out_4(out_11));
  AND_Gate___3 and_3_5 (.in_1(A), .in_2(not_1_out_2), .in_3(not_3_out_2), .out_4(out_13));
  AND_Gate___3 and_3_6 (.in_1(A), .in_2(not_1_out_2), .in_3(C), .out_4(out_15));
  AND_Gate___3 and_3_7 (.in_1(A), .in_2(B), .in_3(not_3_out_2), .out_4(out_17));
  AND_Gate___3 and_3_8 (.in_1(A), .in_2(B), .in_3(C), .out_4(out_19));
  AND_Gate and_1 (.out_3(out_6), .in_1(Data), .in_2(out_5));
  AND_Gate and_2 (.out_3(out_8), .in_1(Data), .in_2(out_7));
  AND_Gate and_3 (.out_3(out_10), .in_1(Data), .in_2(out_9));
  AND_Gate and_4 (.out_3(out_12), .in_1(Data), .in_2(out_11));
  AND_Gate and_5 (.out_3(out_14), .in_1(Data), .in_2(out_13));
  AND_Gate and_6 (.out_3(out_16), .in_1(Data), .in_2(out_15));
  AND_Gate and_7 (.out_3(out_18), .in_1(Data), .in_2(out_17));
  AND_Gate and_8 (.out_3(out_20), .in_1(Data), .in_2(out_19));

  // Notes on the sheet:
  //   B'
  //   A'
  //   C'
endmodule

// Flow Controller
module Flow_Control (
  input  in_1,
  input  in_2,
  input  in_3,
  input  in_4,
  input  in_5,
  input  in_6,
  input  in_7,
  input  in_8,
  input  in_9,
  output out_10,
  output out_11,
  output out_12,
  output out_13,
  output out_14,
  output out_15,
  output out_16,
  output out_17
);

  _8_Bit_AND u_8_bit_and_1 (
    .in_9(in_9), .in_1(in_1), .in_10(in_9), .in_2(in_2), .in_11(in_9), .in_3(in_3), .in_12(in_9),
    .in_4(in_4), .in_13(in_9), .in_5(in_5), .in_14(in_9), .in_6(in_6), .in_15(in_9), .in_7(in_7),
    .Byte_B(in_9), .Byte_A(in_8), .out_17(out_10), .out_18(out_11), .out_19(out_12), .out_20(out_13),
    .out_21(out_14), .out_22(out_15), .out_23(out_16), .out_24(out_17));
endmodule

// Multi Input
module _3_Input_1_Output (
  input  in_1,
  input  in_2,
  input  in_3,
  input  in_4,
  input  in_5,
  input  in_6,
  input  in_7,
  input  in_8,
  input  in_9,
  input  in_10,
  input  in_11,
  input  in_12,
  input  in_13,
  input  in_14,
  input  in_15,
  input  in_16,
  input  in_17,
  input  in_18,
  input  in_19,
  input  in_20,
  input  in_21,
  input  in_22,
  input  in_23,
  input  in_24,
  output out_25,
  output out_26,
  output out_27,
  output out_28,
  output out_29,
  output out_30,
  output out_31,
  output out_32
);

  OR_Gate___3 or_3_1 (.out_4(out_25), .in_1(in_17), .in_2(in_9), .in_3(in_1));
  OR_Gate___3 or_3_2 (.out_4(out_26), .in_1(in_18), .in_2(in_10), .in_3(in_2));
  OR_Gate___3 or_3_3 (.out_4(out_27), .in_1(in_19), .in_2(in_11), .in_3(in_3));
  OR_Gate___3 or_3_4 (.out_4(out_28), .in_1(in_20), .in_2(in_12), .in_3(in_4));
  OR_Gate___3 or_3_5 (.out_4(out_29), .in_1(in_21), .in_2(in_13), .in_3(in_5));
  OR_Gate___3 or_3_6 (.out_4(out_30), .in_1(in_22), .in_2(in_14), .in_3(in_6));
  OR_Gate___3 or_3_7 (.out_4(out_31), .in_1(in_23), .in_2(in_15), .in_3(in_7));
  OR_Gate___3 or_3_8 (.out_4(out_32), .in_1(in_24), .in_2(in_16), .in_3(in_8));
endmodule

module Mux___3 (
  input  in_1,
  input  in_2,
  input  in_3,
  input  in_4,
  input  in_5,
  input  in_6,
  input  in_7,
  input  in_8,
  input  in_9,
  input  in_10,
  input  in_11,
  input  in_12,
  input  in_13,
  input  in_14,
  input  in_15,
  input  in_16,
  input  in_17,
  input  in_18,
  input  in_19,
  input  in_20,
  input  in_21,
  input  in_22,
  input  in_23,
  input  in_24,
  input  in_25,
  input  in_26,
  input  in_27,
  output out_28,
  output out_29,
  output out_30,
  output out_31,
  output out_32,
  output out_33,
  output out_34,
  output out_35
);

  wire flow_control_1_out_10, flow_control_1_out_11, flow_control_1_out_12, flow_control_1_out_13,
       flow_control_1_out_14, flow_control_1_out_15, flow_control_1_out_16, flow_control_1_out_17,
       flow_control_2_out_10, flow_control_2_out_11, flow_control_2_out_12, flow_control_2_out_13,
       flow_control_2_out_14, flow_control_2_out_15, flow_control_2_out_16, flow_control_2_out_17,
       flow_control_3_out_10, flow_control_3_out_11, flow_control_3_out_12, flow_control_3_out_13,
       flow_control_3_out_14, flow_control_3_out_15, flow_control_3_out_16, flow_control_3_out_17;

  Flow_Control flow_control_1 (
    .in_9(in_18), .in_1(in_10), .in_2(in_11), .in_3(in_12), .in_4(in_13), .in_5(in_14), .in_6(in_15),
    .in_7(in_16), .in_8(in_17), .out_10(flow_control_1_out_10), .out_11(flow_control_1_out_11),
    .out_12(flow_control_1_out_12), .out_13(flow_control_1_out_13), .out_14(flow_control_1_out_14),
    .out_15(flow_control_1_out_15), .out_16(flow_control_1_out_16), .out_17(flow_control_1_out_17));
  Flow_Control flow_control_2 (
    .in_9(in_9), .in_1(in_1), .in_2(in_2), .in_3(in_3), .in_4(in_4), .in_5(in_5), .in_6(in_6), .in_7(in_7),
    .in_8(in_8), .out_10(flow_control_2_out_10), .out_11(flow_control_2_out_11),
    .out_12(flow_control_2_out_12), .out_13(flow_control_2_out_13), .out_14(flow_control_2_out_14),
    .out_15(flow_control_2_out_15), .out_16(flow_control_2_out_16), .out_17(flow_control_2_out_17));
  _3_Input_1_Output u_3_input_1_output_1 (
    .in_1(flow_control_1_out_10), .in_2(flow_control_1_out_11), .in_3(flow_control_1_out_12),
    .in_4(flow_control_1_out_13), .in_5(flow_control_1_out_14), .in_6(flow_control_1_out_15),
    .in_7(flow_control_1_out_16), .in_8(flow_control_1_out_17), .in_9(flow_control_2_out_10),
    .in_10(flow_control_2_out_11), .in_11(flow_control_2_out_12), .in_12(flow_control_2_out_13),
    .in_13(flow_control_2_out_14), .in_14(flow_control_2_out_15), .in_15(flow_control_2_out_16),
    .in_16(flow_control_2_out_17), .in_17(flow_control_3_out_10), .in_18(flow_control_3_out_11),
    .in_19(flow_control_3_out_12), .in_20(flow_control_3_out_13), .in_21(flow_control_3_out_14),
    .in_22(flow_control_3_out_15), .in_23(flow_control_3_out_16), .out_25(out_28), .out_26(out_29),
    .out_27(out_30), .out_28(out_31), .out_29(out_32), .out_30(out_33), .out_31(out_34),
    .in_24(flow_control_3_out_17), .out_32(out_35));
  Flow_Control flow_control_3 (
    .in_9(in_27), .in_1(in_19), .in_2(in_20), .in_3(in_21), .in_4(in_22), .in_5(in_23), .in_6(in_24),
    .in_7(in_25), .in_8(in_26), .out_10(flow_control_3_out_10), .out_11(flow_control_3_out_11),
    .out_12(flow_control_3_out_12), .out_13(flow_control_3_out_13), .out_14(flow_control_3_out_14),
    .out_15(flow_control_3_out_15), .out_16(flow_control_3_out_16), .out_17(flow_control_3_out_17));
endmodule

module Shifter (
  input  Input_Bits,
  input  in_2,
  input  in_3,
  input  in_4,
  input  in_5,
  input  in_6,
  input  in_7,
  input  in_8,
  input  in_9,
  output out_10,
  output out_11,
  output out_12,
  output out_13,
  output out_14,
  output out_15,
  output out_16,
  output out_17
);

  wire and_1_out_3, and_3_out_3, and_4_out_3, and_5_out_3, and_6_out_3, and_7_out_3, and_8_out_3,
       and_9_out_3, and_10_out_3, and_11_out_3, and_12_out_3, and_14_out_3, not_1_out_2;

  NOT_Gate not_1 (.out_2(not_1_out_2), .in_1(in_9));
  AND_Gate and_1 (.out_3(and_1_out_3), .in_1(in_9), .in_2(Input_Bits));
  AND_Gate and_2 (.out_3(out_10), .in_1(not_1_out_2), .in_2(in_2));
  AND_Gate and_3 (.out_3(and_3_out_3), .in_1(in_2), .in_2(in_9));
  OR_Gate or_1 (.out_3(out_11), .in_1(and_4_out_3), .in_2(and_1_out_3));
  AND_Gate and_4 (.out_3(and_4_out_3), .in_1(not_1_out_2), .in_2(in_3));
  OR_Gate or_2 (.out_3(out_12), .in_1(and_6_out_3), .in_2(and_3_out_3));
  AND_Gate and_5 (.out_3(and_5_out_3), .in_1(in_3), .in_2(in_9));
  AND_Gate and_6 (.out_3(and_6_out_3), .in_1(not_1_out_2), .in_2(in_4));
  OR_Gate or_3 (.out_3(out_13), .in_1(and_8_out_3), .in_2(and_5_out_3));
  AND_Gate and_7 (.out_3(and_7_out_3), .in_1(in_4), .in_2(in_9));
  AND_Gate and_8 (.out_3(and_8_out_3), .in_1(not_1_out_2), .in_2(in_5));
  AND_Gate and_9 (.out_3(and_9_out_3), .in_1(in_5), .in_2(in_9));
  OR_Gate or_4 (.out_3(out_14), .in_1(and_10_out_3), .in_2(and_7_out_3));
  AND_Gate and_10 (.out_3(and_10_out_3), .in_1(not_1_out_2), .in_2(in_6));
  AND_Gate and_11 (.out_3(and_11_out_3), .in_1(in_6), .in_2(in_9));
  OR_Gate or_5 (.out_3(out_15), .in_1(and_12_out_3), .in_2(and_9_out_3));
  AND_Gate and_12 (.out_3(and_12_out_3), .in_1(not_1_out_2), .in_2(in_7));
  OR_Gate or_6 (.out_3(out_16), .in_1(and_14_out_3), .in_2(and_11_out_3));
  AND_Gate and_13 (.out_3(out_17), .in_1(in_7), .in_2(in_9));
  AND_Gate and_14 (.out_3(and_14_out_3), .in_1(not_1_out_2), .in_2(in_8));

  // Notes on the sheet:
  //   0 - Left
  //   1 - Right
  //   Direction Bit
  //   Output Bits
endmodule

// L Shift
module Left_Shifter (
  input  in_1,
  input  in_2,
  input  in_3,
  input  in_4,
  input  in_5,
  input  in_6,
  input  in_7,
  input  in_8,
  output out_9,
  output out_10,
  output out_11,
  output out_12,
  output out_13,
  output out_14,
  output out_15,
  output out_16
);

  // Probe on in_1

  assign out_9 = in_2;
  assign out_10 = in_3;
  assign out_11 = in_4;
  assign out_12 = in_5;
  assign out_13 = in_6;
  assign out_14 = in_7;
  assign out_15 = in_8;
  assign out_16 = 1'b0;
endmodule

// R Shift
module Right_Shifter (
  input  in_1,
  input  in_2,
  input  in_3,
  input  in_4,
  input  in_5,
  input  in_6,
  input  in_7,
  input  in_8,
  output out_9,
  output out_10,
  output out_11,
  output out_12,
  output out_13,
  output out_14,
  output out_15,
  output out_16
);

  // Probe on in_8

  assign out_9 = 1'b0;
  assign out_10 = in_1;
  assign out_11 = in_2;
  assign out_12 = in_3;
  assign out_13 = in_4;
  assign out_14 = in_5;
  assign out_15 = in_6;
  assign out_16 = in_7;
endmodule

// L Shifter
module Barrel_Shifter__Left (
  input  in_1,
  input  in_2,
  input  in_3,
  input  in_4,
  input  in_5,
  input  in_6,
  input  in_7,
  input  in_8,
  input  in_9,
  input  in_10,
  input  in_11,
  input  in_12,
  output out_13,
  output out_14,
  output out_15,
  output out_16,
  output out_17,
  output out_18,
  output out_19,
  output out_20
);

  wire decoder_3_8_1_out_4, decoder_3_8_1_out_5, decoder_3_8_1_out_6, decoder_3_8_1_out_7,
       decoder_3_8_1_out_8, decoder_3_8_1_out_9, decoder_3_8_1_out_10, decoder_3_8_1_out_11,
       left_shifter_1_out_9, left_shifter_1_out_10, left_shifter_1_out_11, left_shifter_1_out_12,
       left_shifter_1_out_13, left_shifter_1_out_14, left_shifter_1_out_15, left_shifter_1_out_16,
       left_shifter_2_out_9, left_shifter_2_out_10, left_shifter_2_out_11, left_shifter_2_out_12,
       left_shifter_2_out_13, left_shifter_2_out_14, left_shifter_2_out_15, left_shifter_2_out_16,
       left_shifter_3_out_9, left_shifter_3_out_10, left_shifter_3_out_11, left_shifter_3_out_12,
       left_shifter_3_out_13, left_shifter_3_out_14, left_shifter_3_out_15, left_shifter_3_out_16,
       left_shifter_4_out_9, left_shifter_4_out_10, left_shifter_4_out_11, left_shifter_4_out_12,
       left_shifter_4_out_13, left_shifter_4_out_14, left_shifter_4_out_15, left_shifter_4_out_16,
       left_shifter_5_out_9, left_shifter_5_out_10, left_shifter_5_out_11, left_shifter_5_out_12,
       left_shifter_5_out_13, left_shifter_5_out_14, left_shifter_5_out_15, left_shifter_5_out_16,
       left_shifter_6_out_9, left_shifter_6_out_10, left_shifter_6_out_11, left_shifter_6_out_12,
       left_shifter_6_out_13, left_shifter_6_out_14, left_shifter_6_out_15, left_shifter_6_out_16,
       left_shifter_7_out_9, left_shifter_7_out_10, left_shifter_7_out_11, left_shifter_7_out_12,
       left_shifter_7_out_13, left_shifter_7_out_14, left_shifter_7_out_15, left_shifter_7_out_16,
       left_shifter_8_out_9, left_shifter_8_out_10, left_shifter_8_out_11, left_shifter_8_out_12,
       left_shifter_8_out_13, left_shifter_8_out_14, left_shifter_8_out_15, left_shifter_8_out_16,
       mux_4_1_out_37, mux_4_1_out_38, mux_4_1_out_39, mux_4_1_out_40, mux_4_1_out_41, mux_4_1_out_42,
       mux_4_1_out_43, mux_4_1_out_44, mux_4_2_out_37, mux_4_2_out_38, mux_4_2_out_39, mux_4_2_out_40,
       mux_4_2_out_41, mux_4_2_out_42, mux_4_2_out_43, mux_4_2_out_44;

  // Probe on in_1
  Decoder_3_8 decoder_3_8_1 (
    .out_4(decoder_3_8_1_out_4), .out_5(decoder_3_8_1_out_5), .out_6(decoder_3_8_1_out_6),
    .out_7(decoder_3_8_1_out_7), .out_8(decoder_3_8_1_out_8), .out_9(decoder_3_8_1_out_9),
    .out_10(decoder_3_8_1_out_10), .out_11(decoder_3_8_1_out_11), .A(in_2), .B(in_3), .C(in_4));
  Left_Shifter left_shifter_1 (
    .in_1(in_5), .in_2(in_6), .in_3(in_7), .in_4(in_8), .in_5(in_9), .in_6(in_10), .in_7(in_11),
    .in_8(in_12), .out_9(left_shifter_1_out_9), .out_10(left_shifter_1_out_10),
    .out_11(left_shifter_1_out_11), .out_12(left_shifter_1_out_12), .out_13(left_shifter_1_out_13),
    .out_14(left_shifter_1_out_14), .out_15(left_shifter_1_out_15), .out_16(left_shifter_1_out_16));
  Left_Shifter left_shifter_2 (
    .in_1(in_9), .in_2(in_10), .in_3(in_11), .in_4(in_12), .in_5(1'b0), .in_6(1'b0), .in_7(1'b0),
    .in_8(1'b0), .out_9(left_shifter_2_out_9), .out_10(left_shifter_2_out_10),
    .out_11(left_shifter_2_out_11), .out_12(left_shifter_2_out_12), .out_13(left_shifter_2_out_13),
    .out_14(left_shifter_2_out_14), .out_15(left_shifter_2_out_15), .out_16(left_shifter_2_out_16));
  Left_Shifter left_shifter_3 (
    .in_1(in_6), .in_2(in_7), .in_3(in_8), .in_4(in_9), .in_5(in_10), .in_6(in_11), .in_7(in_12),
    .in_8(1'b0), .out_9(left_shifter_3_out_9), .out_10(left_shifter_3_out_10),
    .out_11(left_shifter_3_out_11), .out_12(left_shifter_3_out_12), .out_13(left_shifter_3_out_13),
    .out_14(left_shifter_3_out_14), .out_15(left_shifter_3_out_15), .out_16(left_shifter_3_out_16));
  Mux___4 mux_4_1 (
    .in_9(decoder_3_8_1_out_4), .in_18(decoder_3_8_1_out_5), .in_27(decoder_3_8_1_out_6),
    .in_10(left_shifter_3_out_9), .in_11(left_shifter_3_out_10), .in_12(left_shifter_3_out_11),
    .in_13(left_shifter_3_out_12), .in_14(left_shifter_3_out_13), .in_15(left_shifter_3_out_14),
    .in_16(left_shifter_3_out_15), .in_17(left_shifter_3_out_16), .in_1(left_shifter_1_out_9),
    .in_2(left_shifter_1_out_10), .in_3(left_shifter_1_out_11), .in_4(left_shifter_1_out_12),
    .in_5(left_shifter_1_out_13), .in_6(left_shifter_1_out_14), .in_7(left_shifter_1_out_15),
    .in_8(left_shifter_1_out_16), .in_19(left_shifter_5_out_9), .in_28(left_shifter_7_out_9),
    .in_20(left_shifter_5_out_10), .in_29(left_shifter_7_out_10), .in_21(left_shifter_5_out_11),
    .in_30(left_shifter_7_out_11), .in_22(left_shifter_5_out_12), .in_31(left_shifter_7_out_12),
    .in_23(left_shifter_5_out_13), .in_32(left_shifter_7_out_13), .in_24(left_shifter_5_out_14),
    .in_33(left_shifter_7_out_14), .in_25(left_shifter_5_out_15), .in_34(left_shifter_7_out_15),
    .in_26(left_shifter_5_out_16), .in_35(left_shifter_7_out_16), .out_37(mux_4_1_out_37),
    .out_38(mux_4_1_out_38), .out_39(mux_4_1_out_39), .out_40(mux_4_1_out_40), .out_41(mux_4_1_out_41),
    .out_42(mux_4_1_out_42), .out_43(mux_4_1_out_43), .out_44(mux_4_1_out_44), .in_36(decoder_3_8_1_out_7));
  Left_Shifter left_shifter_4 (
    .in_1(in_10), .in_2(in_11), .in_3(in_12), .in_4(1'b0), .in_5(1'b0), .in_6(1'b0), .in_7(1'b0),
    .in_8(1'b0), .out_9(left_shifter_4_out_9), .out_10(left_shifter_4_out_10),
    .out_11(left_shifter_4_out_11), .out_12(left_shifter_4_out_12), .out_13(left_shifter_4_out_13),
    .out_14(left_shifter_4_out_14), .out_15(left_shifter_4_out_15), .out_16(left_shifter_4_out_16));
  Mux___4 mux_4_2 (
    .in_9(decoder_3_8_1_out_8), .in_18(decoder_3_8_1_out_9), .in_27(decoder_3_8_1_out_10),
    .in_10(left_shifter_4_out_9), .in_11(left_shifter_4_out_10), .in_12(left_shifter_4_out_11),
    .in_13(left_shifter_4_out_12), .in_14(left_shifter_4_out_13), .in_15(left_shifter_4_out_14),
    .in_16(left_shifter_4_out_15), .in_17(left_shifter_4_out_16), .in_1(left_shifter_2_out_9),
    .in_2(left_shifter_2_out_10), .in_3(left_shifter_2_out_11), .in_4(left_shifter_2_out_12),
    .in_5(left_shifter_2_out_13), .in_6(left_shifter_2_out_14), .in_7(left_shifter_2_out_15),
    .in_8(left_shifter_2_out_16), .in_19(left_shifter_6_out_9), .in_28(left_shifter_8_out_9),
    .in_20(left_shifter_6_out_10), .in_29(left_shifter_8_out_10), .in_21(left_shifter_6_out_11),
    .in_30(left_shifter_8_out_11), .in_22(left_shifter_6_out_12), .in_31(left_shifter_8_out_12),
    .in_23(left_shifter_6_out_13), .in_32(left_shifter_8_out_13), .in_24(left_shifter_6_out_14),
    .in_33(left_shifter_8_out_14), .in_25(left_shifter_6_out_15), .in_34(left_shifter_8_out_15),
    .in_26(left_shifter_6_out_16), .in_35(left_shifter_8_out_16), .out_37(mux_4_2_out_37),
    .out_38(mux_4_2_out_38), .out_39(mux_4_2_out_39), .out_40(mux_4_2_out_40), .out_41(mux_4_2_out_41),
    .out_42(mux_4_2_out_42), .out_43(mux_4_2_out_43), .out_44(mux_4_2_out_44), .in_36(decoder_3_8_1_out_11));
  Left_Shifter left_shifter_5 (
    .in_1(in_7), .in_2(in_8), .in_3(in_9), .in_4(in_10), .in_5(in_11), .in_6(in_12), .in_7(1'b0),
    .in_8(1'b0), .out_9(left_shifter_5_out_9), .out_10(left_shifter_5_out_10),
    .out_11(left_shifter_5_out_11), .out_12(left_shifter_5_out_12), .out_13(left_shifter_5_out_13),
    .out_14(left_shifter_5_out_14), .out_15(left_shifter_5_out_15), .out_16(left_shifter_5_out_16));
  Left_Shifter left_shifter_6 (
    .in_1(in_11), .in_2(in_12), .in_3(1'b0), .in_4(1'b0), .in_5(1'b0), .in_6(1'b0), .in_7(1'b0), .in_8(1'b0),
    .out_9(left_shifter_6_out_9), .out_10(left_shifter_6_out_10), .out_11(left_shifter_6_out_11),
    .out_12(left_shifter_6_out_12), .out_13(left_shifter_6_out_13), .out_14(left_shifter_6_out_14),
    .out_15(left_shifter_6_out_15), .out_16(left_shifter_6_out_16));
  Left_Shifter left_shifter_7 (
    .in_1(in_8), .in_2(in_9), .in_3(in_10), .in_4(in_11), .in_5(in_12), .in_6(1'b0), .in_7(1'b0),
    .in_8(1'b0), .out_9(left_shifter_7_out_9), .out_10(left_shifter_7_out_10),
    .out_11(left_shifter_7_out_11), .out_12(left_shifter_7_out_12), .out_13(left_shifter_7_out_13),
    .out_14(left_shifter_7_out_14), .out_15(left_shifter_7_out_15), .out_16(left_shifter_7_out_16));
  Left_Shifter left_shifter_8 (
    .in_1(in_12), .in_2(1'b0), .in_3(1'b0), .in_4(1'b0), .in_5(1'b0), .in_6(1'b0), .in_7(1'b0), .in_8(1'b0),
    .out_9(left_shifter_8_out_9), .out_10(left_shifter_8_out_10), .out_11(left_shifter_8_out_11),
    .out_12(left_shifter_8_out_12), .out_13(left_shifter_8_out_13), .out_14(left_shifter_8_out_14),
    .out_15(left_shifter_8_out_15), .out_16(left_shifter_8_out_16));
  Mux___2 mux_2_1 (
    .in_9(1'b1), .in_18(1'b1), .in_10(mux_4_1_out_37), .in_11(mux_4_1_out_38), .in_12(mux_4_1_out_39),
    .in_13(mux_4_1_out_40), .in_14(mux_4_1_out_41), .in_15(mux_4_1_out_42), .in_16(mux_4_1_out_43),
    .in_17(mux_4_1_out_44), .in_1(mux_4_2_out_37), .in_2(mux_4_2_out_38), .in_3(mux_4_2_out_39),
    .in_4(mux_4_2_out_40), .in_5(mux_4_2_out_41), .in_6(mux_4_2_out_42), .in_7(mux_4_2_out_43),
    .in_8(mux_4_2_out_44), .out_19(out_13), .out_20(out_14), .out_21(out_15), .out_22(out_16),
    .out_23(out_17), .out_24(out_18), .out_25(out_19), .out_26(out_20));
endmodule

// R Shifter
module Barrel_Shifter__Right (
  input  in_1,
  input  in_2,
  input  in_3,
  input  in_4,
  input  in_5,
  input  in_6,
  input  in_7,
  input  in_8,
  input  in_9,
  input  in_10,
  input  in_11,
  input  in_12,
  output out_13,
  output out_14,
  output out_15,
  output out_16,
  output out_17,
  output out_18,
  output out_19,
  output out_20
);

  wire decoder_3_8_1_out_4, decoder_3_8_1_out_5, decoder_3_8_1_out_6, decoder_3_8_1_out_7,
       decoder_3_8_1_out_8, decoder_3_8_1_out_9, decoder_3_8_1_out_10, decoder_3_8_1_out_11, mux_4_1_out_37,
       mux_4_1_out_38, mux_4_1_out_39, mux_4_1_out_40, mux_4_1_out_41, mux_4_1_out_42, mux_4_1_out_43,
       mux_4_1_out_44, mux_4_2_out_37, mux_4_2_out_38, mux_4_2_out_39, mux_4_2_out_40, mux_4_2_out_41,
       mux_4_2_out_42, mux_4_2_out_43, mux_4_2_out_44, right_shifter_1_out_9, right_shifter_1_out_10,
       right_shifter_1_out_11, right_shifter_1_out_12, right_shifter_1_out_13, right_shifter_1_out_14,
       right_shifter_1_out_15, right_shifter_1_out_16, right_shifter_2_out_9, right_shifter_2_out_10,
       right_shifter_2_out_11, right_shifter_2_out_12, right_shifter_2_out_13, right_shifter_2_out_14,
       right_shifter_2_out_15, right_shifter_2_out_16, right_shifter_3_out_9, right_shifter_3_out_10,
       right_shifter_3_out_11, right_shifter_3_out_12, right_shifter_3_out_13, right_shifter_3_out_14,
       right_shifter_3_out_15, right_shifter_3_out_16, right_shifter_4_out_9, right_shifter_4_out_10,
       right_shifter_4_out_11, right_shifter_4_out_12, right_shifter_4_out_13, right_shifter_4_out_14,
       right_shifter_4_out_15, right_shifter_4_out_16, right_shifter_5_out_9, right_shifter_5_out_10,
       right_shifter_5_out_11, right_shifter_5_out_12, right_shifter_5_out_13, right_shifter_5_out_14,
       right_shifter_5_out_15, right_shifter_5_out_16, right_shifter_6_out_9, right_shifter_6_out_10,
       right_shifter_6_out_11, right_shifter_6_out_12, right_shifter_6_out_13, right_shifter_6_out_14,
       right_shifter_6_out_15, right_shifter_6_out_16, right_shifter_7_out_9, right_shifter_7_out_10,
       right_shifter_7_out_11, right_shifter_7_out_12, right_shifter_7_out_13, right_shifter_7_out_14,
       right_shifter_7_out_15, right_shifter_7_out_16, right_shifter_8_out_9, right_shifter_8_out_10,
       right_shifter_8_out_11, right_shifter_8_out_12, right_shifter_8_out_13, right_shifter_8_out_14,
       right_shifter_8_out_15, right_shifter_8_out_16;

  // Probe on in_1
  Decoder_3_8 decoder_3_8_1 (
    .out_4(decoder_3_8_1_out_4), .out_5(decoder_3_8_1_out_5), .out_6(decoder_3_8_1_out_6),
    .out_7(decoder_3_8_1_out_7), .out_8(decoder_3_8_1_out_8), .out_9(decoder_3_8_1_out_9),
    .out_10(decoder_3_8_1_out_10), .out_11(decoder_3_8_1_out_11), .A(in_2), .B(in_3), .C(in_4));
  Right_Shifter right_shifter_1 (
    .in_1(in_5), .in_2(in_6), .in_3(in_7), .in_4(in_8), .in_5(in_9), .in_6(in_10), .in_7(in_11),
    .in_8(in_12), .out_9(right_shifter_1_out_9), .out_10(right_shifter_1_out_10),
    .out_11(right_shifter_1_out_11), .out_12(right_shifter_1_out_12), .out_13(right_shifter_1_out_13),
    .out_14(right_shifter_1_out_14), .out_15(right_shifter_1_out_15), .out_16(right_shifter_1_out_16));
  Right_Shifter right_shifter_2 (
    .in_1(1'b0), .in_2(1'b0), .in_3(1'b0), .in_4(1'b0), .in_5(in_5), .in_6(in_6), .in_7(in_7), .in_8(in_8),
    .out_9(right_shifter_2_out_9), .out_10(right_shifter_2_out_10), .out_11(right_shifter_2_out_11),
    .out_12(right_shifter_2_out_12), .out_13(right_shifter_2_out_13), .out_14(right_shifter_2_out_14),
    .out_15(right_shifter_2_out_15), .out_16(right_shifter_2_out_16));
  Right_Shifter right_shifter_3 (
    .in_1(1'b0), .in_2(in_5), .in_3(in_6), .in_4(in_7), .in_5(in_8), .in_6(in_9), .in_7(in_10), .in_8(in_11),
    .out_9(right_shifter_3_out_9), .out_10(right_shifter_3_out_10), .out_11(right_shifter_3_out_11),
    .out_12(right_shifter_3_out_12), .out_13(right_shifter_3_out_13), .out_14(right_shifter_3_out_14),
    .out_15(right_shifter_3_out_15), .out_16(right_shifter_3_out_16));
  Mux___4 mux_4_1 (
    .in_9(decoder_3_8_1_out_4), .in_18(decoder_3_8_1_out_5), .in_27(decoder_3_8_1_out_6),
    .in_10(right_shifter_3_out_9), .in_11(right_shifter_3_out_10), .in_12(right_shifter_3_out_11),
    .in_13(right_shifter_3_out_12), .in_14(right_shifter_3_out_13), .in_15(right_shifter_3_out_14),
    .in_16(right_shifter_3_out_15), .in_17(right_shifter_3_out_16), .in_1(right_shifter_1_out_9),
    .in_2(right_shifter_1_out_10), .in_3(right_shifter_1_out_11), .in_4(right_shifter_1_out_12),
    .in_5(right_shifter_1_out_13), .in_6(right_shifter_1_out_14), .in_7(right_shifter_1_out_15),
    .in_8(right_shifter_1_out_16), .in_19(right_shifter_5_out_9), .in_28(right_shifter_7_out_9),
    .in_20(right_shifter_5_out_10), .in_29(right_shifter_7_out_10), .in_21(right_shifter_5_out_11),
    .in_30(right_shifter_7_out_11), .in_22(right_shifter_5_out_12), .in_31(right_shifter_7_out_12),
    .in_23(right_shifter_5_out_13), .in_32(right_shifter_7_out_13), .in_24(right_shifter_5_out_14),
    .in_33(right_shifter_7_out_14), .in_25(right_shifter_5_out_15), .in_34(right_shifter_7_out_15),
    .in_26(right_shifter_5_out_16), .in_35(right_shifter_7_out_16), .out_37(mux_4_1_out_37),
    .out_38(mux_4_1_out_38), .out_39(mux_4_1_out_39), .out_40(mux_4_1_out_40), .out_41(mux_4_1_out_41),
    .out_42(mux_4_1_out_42), .out_43(mux_4_1_out_43), .out_44(mux_4_1_out_44), .in_36(decoder_3_8_1_out_7));
  Right_Shifter right_shifter_4 (
    .in_1(1'b0), .in_2(1'b0), .in_3(1'b0), .in_4(1'b0), .in_5(1'b0), .in_6(in_5), .in_7(in_6), .in_8(in_7),
    .out_9(right_shifter_4_out_9), .out_10(right_shifter_4_out_10), .out_11(right_shifter_4_out_11),
    .out_12(right_shifter_4_out_12), .out_13(right_shifter_4_out_13), .out_14(right_shifter_4_out_14),
    .out_15(right_shifter_4_out_15), .out_16(right_shifter_4_out_16));
  Mux___4 mux_4_2 (
    .in_9(decoder_3_8_1_out_8), .in_18(decoder_3_8_1_out_9), .in_27(decoder_3_8_1_out_10),
    .in_10(right_shifter_4_out_9), .in_11(right_shifter_4_out_10), .in_12(right_shifter_4_out_11),
    .in_13(right_shifter_4_out_12), .in_14(right_shifter_4_out_13), .in_15(right_shifter_4_out_14),
    .in_16(right_shifter_4_out_15), .in_17(right_shifter_4_out_16), .in_1(right_shifter_2_out_9),
    .in_2(right_shifter_2_out_10), .in_3(right_shifter_2_out_11), .in_4(right_shifter_2_out_12),
    .in_5(right_shifter_2_out_13), .in_6(right_shifter_2_out_14), .in_7(right_shifter_2_out_15),
    .in_8(right_shifter_2_out_16), .in_19(right_shifter_6_out_9), .in_28(right_shifter_8_out_9),
    .in_20(right_shifter_6_out_10), .in_29(right_shifter_8_out_10), .in_21(right_shifter_6_out_11),
    .in_30(right_shifter_8_out_11), .in_22(right_shifter_6_out_12), .in_31(right_shifter_8_out_12),
    .in_23(right_shifter_6_out_13), .in_32(right_shifter_8_out_13), .in_24(right_shifter_6_out_14),
    .in_33(right_shifter_8_out_14), .in_25(right_shifter_6_out_15), .in_34(right_shifter_8_out_15),
    .in_26(right_shifter_6_out_16), .in_35(right_shifter_8_out_16), .out_37(mux_4_2_out_37),
    .out_38(mux_4_2_out_38), .out_39(mux_4_2_out_39), .out_40(mux_4_2_out_40), .out_41(mux_4_2_out_41),
    .out_42(mux_4_2_out_42), .out_43(mux_4_2_out_43), .out_44(mux_4_2_out_44), .in_36(decoder_3_8_1_out_11));
  Right_Shifter right_shifter_5 (
    .in_1(1'b0), .in_2(1'b0), .in_3(in_5), .in_4(in_6), .in_5(in_7), .in_6(in_8), .in_7(in_9), .in_8(in_10),
    .out_9(right_shifter_5_out_9), .out_10(right_shifter_5_out_10), .out_11(right_shifter_5_out_11),
    .out_12(right_shifter_5_out_12), .out_13(right_shifter_5_out_13), .out_14(right_shifter_5_out_14),
    .out_15(right_shifter_5_out_15), .out_16(right_shifter_5_out_16));
  Right_Shifter right_shifter_6 (
    .in_1(1'b0), .in_2(1'b0), .in_3(1'b0), .in_4(1'b0), .in_5(1'b0), .in_6(1'b0), .in_7(in_5), .in_8(in_6),
    .out_9(right_shifter_6_out_9), .out_10(right_shifter_6_out_10), .out_11(right_shifter_6_out_11),
    .out_12(right_shifter_6_out_12), .out_13(right_shifter_6_out_13), .out_14(right_shifter_6_out_14),
    .out_15(right_shifter_6_out_15), .out_16(right_shifter_6_out_16));
  Right_Shifter right_shifter_7 (
    .in_1(1'b0), .in_2(1'b0), .in_3(1'b0), .in_4(in_5), .in_5(in_6), .in_6(in_7), .in_7(in_8), .in_8(in_9),
    .out_9(right_shifter_7_out_9), .out_10(right_shifter_7_out_10), .out_11(right_shifter_7_out_11),
    .out_12(right_shifter_7_out_12), .out_13(right_shifter_7_out_13), .out_14(right_shifter_7_out_14),
    .out_15(right_shifter_7_out_15), .out_16(right_shifter_7_out_16));
  Right_Shifter right_shifter_8 (
    .in_1(1'b0), .in_2(1'b0), .in_3(1'b0), .in_4(1'b0), .in_5(1'b0), .in_6(1'b0), .in_7(1'b0), .in_8(in_5),
    .out_9(right_shifter_8_out_9), .out_10(right_shifter_8_out_10), .out_11(right_shifter_8_out_11),
    .out_12(right_shifter_8_out_12), .out_13(right_shifter_8_out_13), .out_14(right_shifter_8_out_14),
    .out_15(right_shifter_8_out_15), .out_16(right_shifter_8_out_16));
  Mux___2 mux_2_1 (
    .in_9(1'b1), .in_18(1'b1), .in_10(mux_4_1_out_37), .in_11(mux_4_1_out_38), .in_12(mux_4_1_out_39),
    .in_13(mux_4_1_out_40), .in_14(mux_4_1_out_41), .in_15(mux_4_1_out_42), .in_16(mux_4_1_out_43),
    .in_17(mux_4_1_out_44), .in_1(mux_4_2_out_37), .in_2(mux_4_2_out_38), .in_3(mux_4_2_out_39),
    .in_4(mux_4_2_out_40), .in_5(mux_4_2_out_41), .in_6(mux_4_2_out_42), .in_7(mux_4_2_out_43),
    .in_8(mux_4_2_out_44), .out_19(out_13), .out_20(out_14), .out_21(out_15), .out_22(out_16),
    .out_23(out_17), .out_24(out_18), .out_25(out_19), .out_26(out_20));
endmodule

module ALU (
  input  [3:0] in_1,
  input  Input_Bus_1,
  input  in_3,
  input  in_4,
  input  in_5,
  input  in_6,
  input  in_7,
  input  in_8,
  input  in_9,
  input  Input_Bus_2,
  input  in_11,
  input  in_12,
  input  in_13,
  input  in_14,
  input  in_15,
  input  in_16,
  input  in_17,
  input  Subtract,
  input  Add,
  input  XOR,
  input  AND,
  input  No_Shift,
  input  Left_Shift,
  input  Right_Shift,
  output Output_Bus,
  output out_26,
  output out_27,
  output out_28,
  output out_29,
  output out_30,
  output out_31,
  output out_32
);

  wire and_1_out_3, barrel_shifter_left_1_out_13, barrel_shifter_left_1_out_14, barrel_shifter_left_1_out_15,
       barrel_shifter_left_1_out_16, barrel_shifter_left_1_out_17, barrel_shifter_left_1_out_18,
       barrel_shifter_left_1_out_19, barrel_shifter_left_1_out_20, barrel_shifter_right_1_out_13,
       barrel_shifter_right_1_out_14, barrel_shifter_right_1_out_15, barrel_shifter_right_1_out_16,
       barrel_shifter_right_1_out_17, barrel_shifter_right_1_out_18, barrel_shifter_right_1_out_19,
       barrel_shifter_right_1_out_20, mux_3_1_out_28, mux_3_1_out_29, mux_3_1_out_30, mux_3_1_out_31,
       mux_3_1_out_32, mux_3_1_out_33, mux_3_1_out_34, mux_3_1_out_35, mux_3_2_out_28, mux_3_2_out_29,
       mux_3_2_out_30, mux_3_2_out_31, mux_3_2_out_32, mux_3_2_out_33, mux_3_2_out_34, mux_3_2_out_35,
       n8_bit_adder_subtractor_1_p4, n8_bit_adder_subtractor_1_p7, n8_bit_adder_subtractor_1_p9,
       n8_bit_adder_subtractor_1_p10, n8_bit_adder_subtractor_1_p11, n8_bit_adder_subtractor_1_p13,
       n8_bit_adder_subtractor_1_p15, n8_bit_adder_subtractor_1_p17, n8_bit_and_1_out_17,
       n8_bit_and_1_out_18, n8_bit_and_1_out_19, n8_bit_and_1_out_20, n8_bit_and_1_out_21,
       n8_bit_and_1_out_22, n8_bit_and_1_out_23, n8_bit_and_1_out_24, n8_bit_xor_1_out_17,
       n8_bit_xor_1_out_18, n8_bit_xor_1_out_19, n8_bit_xor_1_out_20, n8_bit_xor_1_out_21,
       n8_bit_xor_1_out_22, n8_bit_xor_1_out_23, n8_bit_xor_1_out_24, not_1_out_2, not_2_out_2, or_1_out_3,
       or_2_out_3, undriven;

  NOT_Gate not_1 (.out_2(not_1_out_2), .in_1(Add));
  AND_Gate and_1 (.out_3(and_1_out_3), .in_1(not_1_out_2), .in_2(Subtract));
  // Probe on undriven
  OR_Gate or_1 (.out_3(or_1_out_3), .in_1(Subtract), .in_2(Add));
  OR_Gate or_2 (.out_3(or_2_out_3), .in_1(Right_Shift), .in_2(Left_Shift));
  // _8_Bit_Adder__Subtractor 8_bit_adder_subtractor_1: pin names not known; wires that end beside it: in_13, in_14, in_15, n8_bit_adder_subtractor_1_p4, in_16, in_16, n8_bit_adder_subtractor_1_p7, in_17, n8_bit_adder_subtractor_1_p9, n8_bit_adder_subtractor_1_p10, n8_bit_adder_subtractor_1_p11, Input_Bus_1, n8_bit_adder_subtractor_1_p13, in_3, n8_bit_adder_subtractor_1_p15, in_4, n8_bit_adder_subtractor_1_p17
  Mux___3 mux_3_1 (
    .in_9(XOR), .in_18(or_1_out_3), .in_27(AND), .in_10(n8_bit_adder_subtractor_1_p4),
    .in_11(n8_bit_adder_subtractor_1_p7), .in_12(n8_bit_adder_subtractor_1_p9),
    .in_13(n8_bit_adder_subtractor_1_p10), .in_14(n8_bit_adder_subtractor_1_p11),
    .in_15(n8_bit_adder_subtractor_1_p13), .in_16(n8_bit_adder_subtractor_1_p15),
    .in_17(n8_bit_adder_subtractor_1_p17), .in_1(n8_bit_xor_1_out_17), .in_2(n8_bit_xor_1_out_18),
    .in_3(n8_bit_xor_1_out_19), .in_4(n8_bit_xor_1_out_20), .in_5(n8_bit_xor_1_out_21),
    .in_6(n8_bit_xor_1_out_22), .in_7(n8_bit_xor_1_out_23), .in_8(n8_bit_xor_1_out_24),
    .in_19(n8_bit_and_1_out_17), .in_20(n8_bit_and_1_out_18), .in_21(n8_bit_and_1_out_19),
    .in_22(n8_bit_and_1_out_20), .in_23(n8_bit_and_1_out_21), .in_24(n8_bit_and_1_out_22),
    .in_25(n8_bit_and_1_out_23), .in_26(n8_bit_and_1_out_24), .out_28(mux_3_1_out_28),
    .out_29(mux_3_1_out_29), .out_30(mux_3_1_out_30), .out_31(mux_3_1_out_31), .out_32(mux_3_1_out_32),
    .out_33(mux_3_1_out_33), .out_34(mux_3_1_out_34), .out_35(mux_3_1_out_35));
  _8_Bit_XOR u_8_bit_xor_1 (
    .in_9(Input_Bus_2), .in_1(Input_Bus_1), .in_10(in_11), .in_2(in_3), .in_11(in_12), .in_3(in_4),
    .in_12(in_13), .in_4(in_5), .in_13(in_14), .in_5(in_6), .in_14(in_15), .in_6(in_7), .in_15(in_16),
    .in_7(in_8), .Byte_B(in_17), .Byte_A(in_9), .out_17(n8_bit_xor_1_out_17), .out_18(n8_bit_xor_1_out_18),
    .out_19(n8_bit_xor_1_out_19), .out_20(n8_bit_xor_1_out_20), .out_21(n8_bit_xor_1_out_21),
    .out_22(n8_bit_xor_1_out_22), .out_23(n8_bit_xor_1_out_23), .out_24(n8_bit_xor_1_out_24));
  NOT_Gate not_2 (.out_2(not_2_out_2), .in_1(or_2_out_3));
  Mux___2 mux_2_1 (
    .in_9(or_2_out_3), .in_18(not_2_out_2), .in_10(mux_3_1_out_28), .in_11(mux_3_1_out_29),
    .in_12(mux_3_1_out_30), .in_13(mux_3_1_out_31), .in_14(mux_3_1_out_32), .in_15(mux_3_1_out_33),
    .in_16(mux_3_1_out_34), .in_17(mux_3_1_out_35), .in_1(mux_3_2_out_28), .in_2(mux_3_2_out_29),
    .in_3(mux_3_2_out_30), .in_4(mux_3_2_out_31), .in_5(mux_3_2_out_32), .in_6(mux_3_2_out_33),
    .in_7(mux_3_2_out_34), .in_8(mux_3_2_out_35), .out_19(Output_Bus), .out_20(out_26), .out_21(out_27),
    .out_22(out_28), .out_23(out_29), .out_24(out_30), .out_25(out_31), .out_26(out_32));
  _8_Bit_AND u_8_bit_and_1 (
    .in_9(Input_Bus_2), .in_1(Input_Bus_1), .in_10(in_11), .in_2(in_3), .in_11(in_12), .in_3(in_4),
    .in_12(in_13), .in_4(in_5), .in_13(in_14), .in_5(in_6), .in_14(in_15), .in_6(in_7), .in_15(in_16),
    .in_7(in_8), .Byte_B(in_17), .Byte_A(in_9), .out_17(n8_bit_and_1_out_17), .out_18(n8_bit_and_1_out_18),
    .out_19(n8_bit_and_1_out_19), .out_20(n8_bit_and_1_out_20), .out_21(n8_bit_and_1_out_21),
    .out_22(n8_bit_and_1_out_22), .out_23(n8_bit_and_1_out_23), .out_24(n8_bit_and_1_out_24));
  Mux___3 mux_3_2 (
    .in_9(Left_Shift), .in_18(No_Shift), .in_27(Right_Shift), .in_10(Input_Bus_1), .in_11(in_3),
    .in_12(in_4), .in_13(in_5), .in_14(in_6), .in_15(in_7), .in_16(in_8), .in_17(in_9),
    .in_1(barrel_shifter_left_1_out_13), .in_2(barrel_shifter_left_1_out_14),
    .in_3(barrel_shifter_left_1_out_15), .in_4(barrel_shifter_left_1_out_16),
    .in_5(barrel_shifter_left_1_out_17), .in_6(barrel_shifter_left_1_out_18),
    .in_7(barrel_shifter_left_1_out_19), .in_8(barrel_shifter_left_1_out_20),
    .in_19(barrel_shifter_right_1_out_13), .in_20(barrel_shifter_right_1_out_14),
    .in_21(barrel_shifter_right_1_out_15), .in_22(barrel_shifter_right_1_out_16),
    .in_23(barrel_shifter_right_1_out_17), .in_24(barrel_shifter_right_1_out_18),
    .in_25(barrel_shifter_right_1_out_19), .in_26(barrel_shifter_right_1_out_20), .out_28(mux_3_2_out_28),
    .out_29(mux_3_2_out_29), .out_30(mux_3_2_out_30), .out_31(mux_3_2_out_31), .out_32(mux_3_2_out_32),
    .out_33(mux_3_2_out_33), .out_34(mux_3_2_out_34), .out_35(mux_3_2_out_35));
  Barrel_Shifter__Left barrel_shifter_left_1 (
    .out_13(barrel_shifter_left_1_out_13), .out_14(barrel_shifter_left_1_out_14),
    .out_15(barrel_shifter_left_1_out_15), .out_16(barrel_shifter_left_1_out_16),
    .out_17(barrel_shifter_left_1_out_17), .out_18(barrel_shifter_left_1_out_18),
    .out_19(barrel_shifter_left_1_out_19), .out_20(barrel_shifter_left_1_out_20), .in_1(in_1[3]),
    .in_2(in_1[2]), .in_3(in_1[1]), .in_4(in_1[0]), .in_5(Input_Bus_1), .in_6(in_3), .in_7(in_4),
    .in_8(in_5), .in_9(in_6), .in_10(in_7), .in_11(in_8), .in_12(in_9));
  Barrel_Shifter__Right barrel_shifter_right_1 (
    .out_13(barrel_shifter_right_1_out_13), .out_14(barrel_shifter_right_1_out_14),
    .out_15(barrel_shifter_right_1_out_15), .out_16(barrel_shifter_right_1_out_16),
    .out_17(barrel_shifter_right_1_out_17), .out_18(barrel_shifter_right_1_out_18),
    .out_19(barrel_shifter_right_1_out_19), .out_20(barrel_shifter_right_1_out_20), .in_1(in_1[3]),
    .in_2(in_1[2]), .in_3(in_1[1]), .in_4(in_1[0]), .in_5(Input_Bus_1), .in_6(in_3), .in_7(in_4),
    .in_8(in_5), .in_9(in_6), .in_10(in_7), .in_11(in_8), .in_12(in_9));
endmodule

module circuit_2_2 (
);


  // Notes on the sheet:
  //   its worth it
endmodule

// SR FF
module SR_Latch__NOR (
  input  R,
  input  S,
  output Q,
  output Q_prime
);

  nor nor_1 (Q, R, Q_prime);
  nor nor_2 (Q_prime, Q, S);
endmodule

// Memory
module Memory_Bit (
  input  Input,
  input  Write,
  output out_3
);

  wire and_1_out_3, and_2_out_3, clock_1_out, not_1_out_2;

  NOT_Gate not_1 (.out_2(not_1_out_2), .in_1(Input));
  AND_Gate and_1 (.out_3(and_1_out_3), .in_1(Write), .in_2(Input));
  Clock clock_1 (.out(clock_1_out));
  AND_Gate and_2 (.out_3(and_2_out_3), .in_1(Write), .in_2(not_1_out_2));
  S_R_Flip_Flop s_r_ff_1 (
    .S(and_1_out_3), .clk(clock_1_out), .R(and_2_out_3), .Q(out_3));  // open: Qn, preset, reset, en

  // Notes on the sheet:
  //   out_3: pull=down
endmodule

// Register - 4
module Register_4_Bit (
  input  in_1,
  input  in_2,
  input  in_3,
  input  in_4,
  input  Write,
  output out_6,
  output out_7,
  output out_8,
  output out_9
);

  Memory_Bit memory_bit_1 (.Input(in_1), .out_3(out_6), .Write(Write));
  Memory_Bit memory_bit_2 (.Input(in_2), .out_3(out_7), .Write(Write));
  Memory_Bit memory_bit_3 (.Input(in_3), .out_3(out_8), .Write(Write));
  Memory_Bit memory_bit_4 (.Input(in_4), .out_3(out_9), .Write(Write));
endmodule

// Register - 6
module Register_6_Bit (
  input  in_1,
  input  in_2,
  input  in_3,
  input  in_4,
  input  in_5,
  input  in_6,
  input  Write,
  output out_8,
  output out_9,
  output out_10,
  output out_11,
  output out_12,
  output out_13
);

  Memory_Bit memory_bit_1 (.Input(in_1), .out_3(out_8), .Write(Write));
  Memory_Bit memory_bit_2 (.Input(in_2), .out_3(out_9), .Write(Write));
  Memory_Bit memory_bit_3 (.Input(in_3), .out_3(out_10), .Write(Write));
  Memory_Bit memory_bit_4 (.Input(in_4), .out_3(out_11), .Write(Write));
  Memory_Bit memory_bit_5 (.Input(in_5), .out_3(out_12), .Write(Write));
  Memory_Bit memory_bit_6 (.Input(in_6), .out_3(out_13), .Write(Write));
endmodule

// Register - 8
module Register_8_Bit (
  input  in_1,
  input  in_2,
  input  in_3,
  input  in_4,
  input  in_5,
  input  in_6,
  input  in_7,
  input  in_8,
  input  Write,
  output out_10,
  output out_11,
  output out_12,
  output out_13,
  output out_14,
  output out_15,
  output out_16,
  output out_17
);

  Memory_Bit memory_bit_1 (.Input(in_1), .out_3(out_10), .Write(Write));
  Memory_Bit memory_bit_2 (.Input(in_2), .out_3(out_11), .Write(Write));
  Memory_Bit memory_bit_3 (.Input(in_3), .out_3(out_12), .Write(Write));
  Memory_Bit memory_bit_4 (.Input(in_4), .out_3(out_13), .Write(Write));
  Memory_Bit memory_bit_5 (.Input(in_5), .out_3(out_14), .Write(Write));
  Memory_Bit memory_bit_6 (.Input(in_6), .out_3(out_15), .Write(Write));
  Memory_Bit memory_bit_7 (.Input(in_7), .out_3(out_16), .Write(Write));
  Memory_Bit memory_bit_8 (.Input(in_8), .out_3(out_17), .Write(Write));
endmodule

// Flow Control
module Flow_Control_6_Bit (
  input  in_1,
  input  in_2,
  input  in_3,
  input  in_4,
  input  in_5,
  input  in_6,
  input  in_7,
  output out_8,
  output out_9,
  output out_10,
  output out_11,
  output out_12,
  output out_13
);

  wire n8_bit_and_1_out_23, n8_bit_and_1_out_24;

  _8_Bit_AND u_8_bit_and_1 (
    .in_9(in_7), .in_1(in_1), .in_10(in_7), .in_2(in_2), .in_11(in_7), .in_3(in_3), .in_12(in_7),
    .in_4(in_4), .in_13(in_7), .in_5(in_5), .in_14(in_7), .in_6(in_6), .in_15(in_7), .in_7(1'b0),
    .Byte_B(in_7), .Byte_A(1'b0), .out_17(out_8), .out_18(out_9), .out_19(out_10), .out_20(out_11),
    .out_21(out_12), .out_22(out_13), .out_23(n8_bit_and_1_out_23), .out_24(n8_bit_and_1_out_24));
  // also tied to GND on the sheet: {n8_bit_and_1_out_23, n8_bit_and_1_out_24}
endmodule

// Memory Bank
module Memory_Bank__6B__4W (
  input  in_1,
  input  in_2,
  input  in_3,
  input  in_4,
  input  in_5,
  input  in_6,
  input  in_7,
  input  in_8,
  input  in_9,
  output out_10,
  output out_11,
  output out_12,
  output out_13,
  output out_14,
  output out_15
);

  wire decoder_demultiplexer_2_4_1_out_4, decoder_demultiplexer_2_4_1_out_5,
       decoder_demultiplexer_2_4_1_out_6, decoder_demultiplexer_2_4_1_out_7,
       decoder_demultiplexer_2_4_1_out_8, decoder_demultiplexer_2_4_1_out_9,
       decoder_demultiplexer_2_4_1_out_10, decoder_demultiplexer_2_4_1_out_11, flow_control_6_bit_1_out_8,
       flow_control_6_bit_1_out_9, flow_control_6_bit_1_out_10, flow_control_6_bit_1_out_11,
       flow_control_6_bit_1_out_12, flow_control_6_bit_1_out_13, flow_control_6_bit_2_out_8,
       flow_control_6_bit_2_out_9, flow_control_6_bit_2_out_10, flow_control_6_bit_2_out_11,
       flow_control_6_bit_2_out_12, flow_control_6_bit_2_out_13, flow_control_6_bit_3_out_8,
       flow_control_6_bit_3_out_9, flow_control_6_bit_3_out_10, flow_control_6_bit_3_out_11,
       flow_control_6_bit_3_out_12, flow_control_6_bit_3_out_13, flow_control_6_bit_4_out_8,
       flow_control_6_bit_4_out_9, flow_control_6_bit_4_out_10, flow_control_6_bit_4_out_11,
       flow_control_6_bit_4_out_12, flow_control_6_bit_4_out_13, n3_input_1_output_1_out_25,
       n3_input_1_output_1_out_26, n3_input_1_output_1_out_27, n3_input_1_output_1_out_28,
       n3_input_1_output_1_out_29, n3_input_1_output_1_out_30, n3_input_1_output_1_out_31,
       n3_input_1_output_1_out_32, n3_input_1_output_2_out_25, n3_input_1_output_2_out_32,
       register_6_bit_1_out_8, register_6_bit_1_out_9, register_6_bit_1_out_10, register_6_bit_1_out_11,
       register_6_bit_1_out_12, register_6_bit_1_out_13, register_6_bit_2_out_8, register_6_bit_2_out_9,
       register_6_bit_2_out_10, register_6_bit_2_out_11, register_6_bit_2_out_12, register_6_bit_2_out_13,
       register_6_bit_3_out_8, register_6_bit_3_out_9, register_6_bit_3_out_10, register_6_bit_3_out_11,
       register_6_bit_3_out_12, register_6_bit_3_out_13, register_6_bit_4_out_8, register_6_bit_4_out_9,
       register_6_bit_4_out_10, register_6_bit_4_out_11, register_6_bit_4_out_12, register_6_bit_4_out_13;

  Decoder__Demultiplexer_2_4 decoder_demultiplexer_2_4_1 (
    .out_4(decoder_demultiplexer_2_4_1_out_4), .out_5(decoder_demultiplexer_2_4_1_out_5),
    .out_6(decoder_demultiplexer_2_4_1_out_6), .out_7(decoder_demultiplexer_2_4_1_out_7),
    .out_8(decoder_demultiplexer_2_4_1_out_8), .out_9(decoder_demultiplexer_2_4_1_out_9),
    .out_10(decoder_demultiplexer_2_4_1_out_10), .out_11(decoder_demultiplexer_2_4_1_out_11), .A(in_8),
    .B(in_9), .Data(in_7));
  Register_6_Bit register_6_bit_1 (
    .Write(decoder_demultiplexer_2_4_1_out_5), .in_1(in_1), .in_2(in_2), .in_3(in_3), .in_4(in_4),
    .in_5(in_5), .in_6(in_6), .out_8(register_6_bit_1_out_8), .out_9(register_6_bit_1_out_9),
    .out_10(register_6_bit_1_out_10), .out_11(register_6_bit_1_out_11), .out_12(register_6_bit_1_out_12),
    .out_13(register_6_bit_1_out_13));
  Flow_Control_6_Bit flow_control_6_bit_1 (
    .in_7(decoder_demultiplexer_2_4_1_out_4), .in_1(register_6_bit_1_out_8), .in_2(register_6_bit_1_out_9),
    .in_3(register_6_bit_1_out_10), .in_4(register_6_bit_1_out_11), .in_5(register_6_bit_1_out_12),
    .in_6(register_6_bit_1_out_13), .out_8(flow_control_6_bit_1_out_8), .out_9(flow_control_6_bit_1_out_9),
    .out_10(flow_control_6_bit_1_out_10), .out_11(flow_control_6_bit_1_out_11),
    .out_12(flow_control_6_bit_1_out_12), .out_13(flow_control_6_bit_1_out_13));
  Register_6_Bit register_6_bit_2 (
    .Write(decoder_demultiplexer_2_4_1_out_7), .in_1(in_1), .in_2(in_2), .in_3(in_3), .in_4(in_4),
    .in_5(in_5), .in_6(in_6), .out_8(register_6_bit_2_out_8), .out_9(register_6_bit_2_out_9),
    .out_10(register_6_bit_2_out_10), .out_11(register_6_bit_2_out_11), .out_12(register_6_bit_2_out_12),
    .out_13(register_6_bit_2_out_13));
  Flow_Control_6_Bit flow_control_6_bit_2 (
    .in_7(decoder_demultiplexer_2_4_1_out_6), .in_1(register_6_bit_2_out_8), .in_2(register_6_bit_2_out_9),
    .in_3(register_6_bit_2_out_10), .in_4(register_6_bit_2_out_11), .in_5(register_6_bit_2_out_12),
    .in_6(register_6_bit_2_out_13), .out_8(flow_control_6_bit_2_out_8), .out_9(flow_control_6_bit_2_out_9),
    .out_10(flow_control_6_bit_2_out_10), .out_11(flow_control_6_bit_2_out_11),
    .out_12(flow_control_6_bit_2_out_12), .out_13(flow_control_6_bit_2_out_13));
  _3_Input_1_Output u_3_input_1_output_1 (
    .in_1(1'b0), .in_2(flow_control_6_bit_1_out_8), .in_3(flow_control_6_bit_1_out_9),
    .in_4(flow_control_6_bit_1_out_10), .in_5(flow_control_6_bit_1_out_11),
    .in_6(flow_control_6_bit_1_out_12), .in_7(flow_control_6_bit_1_out_13), .in_8(1'b0), .in_9(1'b0),
    .in_10(flow_control_6_bit_2_out_8), .in_11(flow_control_6_bit_2_out_9),
    .in_12(flow_control_6_bit_2_out_10), .in_13(flow_control_6_bit_2_out_11),
    .in_14(flow_control_6_bit_2_out_12), .in_15(flow_control_6_bit_2_out_13), .in_16(1'b0), .in_17(1'b0),
    .in_18(flow_control_6_bit_3_out_8), .in_19(flow_control_6_bit_3_out_9),
    .in_20(flow_control_6_bit_3_out_10), .in_21(flow_control_6_bit_3_out_11),
    .in_22(flow_control_6_bit_3_out_12), .in_23(flow_control_6_bit_3_out_13),
    .out_25(n3_input_1_output_1_out_25), .out_26(n3_input_1_output_1_out_26),
    .out_27(n3_input_1_output_1_out_27), .out_28(n3_input_1_output_1_out_28),
    .out_29(n3_input_1_output_1_out_29), .out_30(n3_input_1_output_1_out_30),
    .out_31(n3_input_1_output_1_out_31), .in_24(1'b0), .out_32(n3_input_1_output_1_out_32));
  Register_6_Bit register_6_bit_3 (
    .Write(decoder_demultiplexer_2_4_1_out_9), .in_1(in_1), .in_2(in_2), .in_3(in_3), .in_4(in_4),
    .in_5(in_5), .in_6(in_6), .out_8(register_6_bit_3_out_8), .out_9(register_6_bit_3_out_9),
    .out_10(register_6_bit_3_out_10), .out_11(register_6_bit_3_out_11), .out_12(register_6_bit_3_out_12),
    .out_13(register_6_bit_3_out_13));
  Flow_Control_6_Bit flow_control_6_bit_3 (
    .in_7(decoder_demultiplexer_2_4_1_out_8), .in_1(register_6_bit_3_out_8), .in_2(register_6_bit_3_out_9),
    .in_3(register_6_bit_3_out_10), .in_4(register_6_bit_3_out_11), .in_5(register_6_bit_3_out_12),
    .in_6(register_6_bit_3_out_13), .out_8(flow_control_6_bit_3_out_8), .out_9(flow_control_6_bit_3_out_9),
    .out_10(flow_control_6_bit_3_out_10), .out_11(flow_control_6_bit_3_out_11),
    .out_12(flow_control_6_bit_3_out_12), .out_13(flow_control_6_bit_3_out_13));
  Register_6_Bit register_6_bit_4 (
    .Write(decoder_demultiplexer_2_4_1_out_11), .in_1(in_1), .in_2(in_2), .in_3(in_3), .in_4(in_4),
    .in_5(in_5), .in_6(in_6), .out_8(register_6_bit_4_out_8), .out_9(register_6_bit_4_out_9),
    .out_10(register_6_bit_4_out_10), .out_11(register_6_bit_4_out_11), .out_12(register_6_bit_4_out_12),
    .out_13(register_6_bit_4_out_13));
  Flow_Control_6_Bit flow_control_6_bit_4 (
    .in_7(decoder_demultiplexer_2_4_1_out_10), .in_1(register_6_bit_4_out_8), .in_2(register_6_bit_4_out_9),
    .in_3(register_6_bit_4_out_10), .in_4(register_6_bit_4_out_11), .in_5(register_6_bit_4_out_12),
    .in_6(register_6_bit_4_out_13), .out_8(flow_control_6_bit_4_out_8), .out_9(flow_control_6_bit_4_out_9),
    .out_10(flow_control_6_bit_4_out_10), .out_11(flow_control_6_bit_4_out_11),
    .out_12(flow_control_6_bit_4_out_12), .out_13(flow_control_6_bit_4_out_13));
  _3_Input_1_Output u_3_input_1_output_2 (
    .in_1(1'b0), .in_2(n3_input_1_output_1_out_26), .in_3(n3_input_1_output_1_out_27),
    .in_4(n3_input_1_output_1_out_28), .in_5(n3_input_1_output_1_out_29), .in_6(n3_input_1_output_1_out_30),
    .in_7(n3_input_1_output_1_out_31), .in_8(1'b0), .in_9(1'b0), .in_10(flow_control_6_bit_4_out_8),
    .in_11(flow_control_6_bit_4_out_9), .in_12(flow_control_6_bit_4_out_10),
    .in_13(flow_control_6_bit_4_out_11), .in_14(flow_control_6_bit_4_out_12),
    .in_15(flow_control_6_bit_4_out_13), .in_16(1'b0), .in_17(1'b0), .in_18(1'b0), .in_19(1'b0),
    .in_20(1'b0), .in_21(1'b0), .in_22(1'b0), .in_23(1'b0), .out_25(n3_input_1_output_2_out_25),
    .out_26(out_10), .out_27(out_11), .out_28(out_12), .out_29(out_13), .out_30(out_14), .out_31(out_15),
    .in_24(1'b0), .out_32(n3_input_1_output_2_out_32));
  // also tied to GND on the sheet: {n3_input_1_output_1_out_25, n3_input_1_output_1_out_32, n3_input_1_output_2_out_25, n3_input_1_output_2_out_32}
endmodule

module Mux___4 (
  input  in_1,
  input  in_2,
  input  in_3,
  input  in_4,
  input  in_5,
  input  in_6,
  input  in_7,
  input  in_8,
  input  in_9,
  input  in_10,
  input  in_11,
  input  in_12,
  input  in_13,
  input  in_14,
  input  in_15,
  input  in_16,
  input  in_17,
  input  in_18,
  input  in_19,
  input  in_20,
  input  in_21,
  input  in_22,
  input  in_23,
  input  in_24,
  input  in_25,
  input  in_26,
  input  in_27,
  input  in_28,
  input  in_29,
  input  in_30,
  input  in_31,
  input  in_32,
  input  in_33,
  input  in_34,
  input  in_35,
  input  in_36,
  output out_37,
  output out_38,
  output out_39,
  output out_40,
  output out_41,
  output out_42,
  output out_43,
  output out_44
);

  wire flow_control_1_out_10, flow_control_1_out_11, flow_control_1_out_12, flow_control_1_out_13,
       flow_control_1_out_14, flow_control_1_out_15, flow_control_1_out_16, flow_control_1_out_17,
       flow_control_2_out_10, flow_control_2_out_11, flow_control_2_out_12, flow_control_2_out_13,
       flow_control_2_out_14, flow_control_2_out_15, flow_control_2_out_16, flow_control_2_out_17,
       flow_control_3_out_10, flow_control_3_out_11, flow_control_3_out_12, flow_control_3_out_13,
       flow_control_3_out_14, flow_control_3_out_15, flow_control_3_out_16, flow_control_3_out_17,
       flow_control_4_out_10, flow_control_4_out_11, flow_control_4_out_12, flow_control_4_out_13,
       flow_control_4_out_14, flow_control_4_out_15, flow_control_4_out_16, flow_control_4_out_17,
       n3_input_1_output_1_out_25, n3_input_1_output_1_out_26, n3_input_1_output_1_out_27,
       n3_input_1_output_1_out_28, n3_input_1_output_1_out_29, n3_input_1_output_1_out_30,
       n3_input_1_output_1_out_31, n3_input_1_output_1_out_32;

  Flow_Control flow_control_1 (
    .in_9(in_18), .in_1(in_10), .in_2(in_11), .in_3(in_12), .in_4(in_13), .in_5(in_14), .in_6(in_15),
    .in_7(in_16), .in_8(in_17), .out_10(flow_control_1_out_10), .out_11(flow_control_1_out_11),
    .out_12(flow_control_1_out_12), .out_13(flow_control_1_out_13), .out_14(flow_control_1_out_14),
    .out_15(flow_control_1_out_15), .out_16(flow_control_1_out_16), .out_17(flow_control_1_out_17));
  Flow_Control flow_control_2 (
    .in_9(in_9), .in_1(in_1), .in_2(in_2), .in_3(in_3), .in_4(in_4), .in_5(in_5), .in_6(in_6), .in_7(in_7),
    .in_8(in_8), .out_10(flow_control_2_out_10), .out_11(flow_control_2_out_11),
    .out_12(flow_control_2_out_12), .out_13(flow_control_2_out_13), .out_14(flow_control_2_out_14),
    .out_15(flow_control_2_out_15), .out_16(flow_control_2_out_16), .out_17(flow_control_2_out_17));
  _3_Input_1_Output u_3_input_1_output_1 (
    .in_1(flow_control_1_out_10), .in_2(flow_control_1_out_11), .in_3(flow_control_1_out_12),
    .in_4(flow_control_1_out_13), .in_5(flow_control_1_out_14), .in_6(flow_control_1_out_15),
    .in_7(flow_control_1_out_16), .in_8(flow_control_1_out_17), .in_9(flow_control_2_out_10),
    .in_10(flow_control_2_out_11), .in_11(flow_control_2_out_12), .in_12(flow_control_2_out_13),
    .in_13(flow_control_2_out_14), .in_14(flow_control_2_out_15), .in_15(flow_control_2_out_16),
    .in_16(flow_control_2_out_17), .in_17(flow_control_3_out_10), .in_18(flow_control_3_out_11),
    .in_19(flow_control_3_out_12), .in_20(flow_control_3_out_13), .in_21(flow_control_3_out_14),
    .in_22(flow_control_3_out_15), .in_23(flow_control_3_out_16), .out_25(n3_input_1_output_1_out_25),
    .out_26(n3_input_1_output_1_out_26), .out_27(n3_input_1_output_1_out_27),
    .out_28(n3_input_1_output_1_out_28), .out_29(n3_input_1_output_1_out_29),
    .out_30(n3_input_1_output_1_out_30), .out_31(n3_input_1_output_1_out_31), .in_24(flow_control_3_out_17),
    .out_32(n3_input_1_output_1_out_32));
  _3_Input_1_Output u_3_input_1_output_2 (
    .in_1(1'b0), .in_2(1'b0), .in_3(1'b0), .in_4(1'b0), .in_5(1'b0), .in_6(1'b0), .in_7(1'b0), .in_8(1'b0),
    .in_9(n3_input_1_output_1_out_25), .in_10(n3_input_1_output_1_out_26),
    .in_11(n3_input_1_output_1_out_27), .in_12(n3_input_1_output_1_out_28),
    .in_13(n3_input_1_output_1_out_29), .in_14(n3_input_1_output_1_out_30),
    .in_15(n3_input_1_output_1_out_31), .in_16(n3_input_1_output_1_out_32), .in_17(flow_control_4_out_10),
    .in_18(flow_control_4_out_11), .in_19(flow_control_4_out_12), .in_20(flow_control_4_out_13),
    .in_21(flow_control_4_out_14), .in_22(flow_control_4_out_15), .in_23(flow_control_4_out_16),
    .out_25(out_37), .out_26(out_38), .out_27(out_39), .out_28(out_40), .out_29(out_41), .out_30(out_42),
    .out_31(out_43), .in_24(flow_control_4_out_17), .out_32(out_44));
  Flow_Control flow_control_3 (
    .in_9(in_27), .in_1(in_19), .in_2(in_20), .in_3(in_21), .in_4(in_22), .in_5(in_23), .in_6(in_24),
    .in_7(in_25), .in_8(in_26), .out_10(flow_control_3_out_10), .out_11(flow_control_3_out_11),
    .out_12(flow_control_3_out_12), .out_13(flow_control_3_out_13), .out_14(flow_control_3_out_14),
    .out_15(flow_control_3_out_15), .out_16(flow_control_3_out_16), .out_17(flow_control_3_out_17));
  Flow_Control flow_control_4 (
    .in_9(in_36), .in_1(in_28), .in_2(in_29), .in_3(in_30), .in_4(in_31), .in_5(in_32), .in_6(in_33),
    .in_7(in_34), .in_8(in_35), .out_10(flow_control_4_out_10), .out_11(flow_control_4_out_11),
    .out_12(flow_control_4_out_12), .out_13(flow_control_4_out_13), .out_14(flow_control_4_out_14),
    .out_15(flow_control_4_out_15), .out_16(flow_control_4_out_16), .out_17(flow_control_4_out_17));
endmodule

// Decoder / Demux
module Decoder__Demultiplexer_4_16 (
  input  A,
  input  B,
  input  C,
  input  D,
  input  Data,
  output out_6,
  output out_7,
  output out_8,
  output out_9,
  output out_10,
  output out_11,
  output out_12,
  output out_13,
  output out_14,
  output out_15,
  output out_16,
  output out_17,
  output out_18,
  output out_19,
  output out_20,
  output out_21,
  output out_22,
  output out_23,
  output out_24,
  output out_25,
  output out_26,
  output out_27,
  output out_28,
  output out_29,
  output out_30,
  output out_31,
  output out_32,
  output out_33,
  output out_34,
  output out_35,
  output out_36,
  output out_37
);

  wire not_1_out_2, not_2_out_2, not_3_out_2, not_4_out_2;

  NOT_Gate not_1 (.out_2(not_1_out_2), .in_1(B));
  NOT_Gate not_2 (.out_2(not_2_out_2), .in_1(A));
  NOT_Gate not_3 (.out_2(not_3_out_2), .in_1(C));
  NOT_Gate not_4 (.out_2(not_4_out_2), .in_1(D));
  AND_Gate___4 and_4_1 (.in_1(not_2_out_2), .in_2(not_1_out_2), .in_3(not_3_out_2), .in_4(not_4_out_2), .out_5(out_6));
  AND_Gate___4 and_4_2 (.in_1(not_2_out_2), .in_2(not_1_out_2), .in_3(not_3_out_2), .in_4(D), .out_5(out_8));
  AND_Gate___4 and_4_3 (.in_1(not_2_out_2), .in_2(not_1_out_2), .in_3(C), .in_4(not_4_out_2), .out_5(out_10));
  AND_Gate___4 and_4_4 (.in_1(not_2_out_2), .in_2(not_1_out_2), .in_3(C), .in_4(D), .out_5(out_12));
  AND_Gate___4 and_4_5 (.in_1(not_2_out_2), .in_2(B), .in_3(not_3_out_2), .in_4(not_4_out_2), .out_5(out_14));
  AND_Gate___4 and_4_6 (.in_1(not_2_out_2), .in_2(B), .in_3(not_3_out_2), .in_4(D), .out_5(out_16));
  AND_Gate___4 and_4_7 (.in_1(not_2_out_2), .in_2(B), .in_3(C), .in_4(not_4_out_2), .out_5(out_18));
  AND_Gate___4 and_4_8 (.in_1(not_2_out_2), .in_2(B), .in_3(C), .in_4(D), .out_5(out_20));
  AND_Gate___4 and_4_9 (.in_1(A), .in_2(not_1_out_2), .in_3(not_3_out_2), .in_4(not_4_out_2), .out_5(out_22));
  AND_Gate___4 and_4_10 (.in_1(A), .in_2(not_1_out_2), .in_3(not_3_out_2), .in_4(D), .out_5(out_24));
  AND_Gate___4 and_4_11 (.in_1(A), .in_2(not_1_out_2), .in_3(C), .in_4(not_4_out_2), .out_5(out_26));
  AND_Gate___4 and_4_12 (.in_1(A), .in_2(not_1_out_2), .in_3(C), .in_4(D), .out_5(out_28));
  AND_Gate___4 and_4_13 (.in_1(A), .in_2(B), .in_3(not_3_out_2), .in_4(not_4_out_2), .out_5(out_30));
  AND_Gate___4 and_4_14 (.in_1(A), .in_2(B), .in_3(not_3_out_2), .in_4(D), .out_5(out_32));
  AND_Gate___4 and_4_15 (.in_1(A), .in_2(B), .in_3(C), .in_4(not_4_out_2), .out_5(out_34));
  AND_Gate___4 and_4_16 (.in_1(A), .in_2(B), .in_3(C), .in_4(D), .out_5(out_36));
  AND_Gate and_1 (.out_3(out_7), .in_1(Data), .in_2(out_6));
  AND_Gate and_2 (.out_3(out_9), .in_1(Data), .in_2(out_8));
  AND_Gate and_3 (.out_3(out_11), .in_1(Data), .in_2(out_10));
  AND_Gate and_4 (.out_3(out_13), .in_1(Data), .in_2(out_12));
  AND_Gate and_5 (.out_3(out_15), .in_1(Data), .in_2(out_14));
  AND_Gate and_6 (.out_3(out_17), .in_1(Data), .in_2(out_16));
  AND_Gate and_7 (.out_3(out_19), .in_1(Data), .in_2(out_18));
  AND_Gate and_8 (.out_3(out_21), .in_1(Data), .in_2(out_20));
  AND_Gate and_9 (.out_3(out_23), .in_1(Data), .in_2(out_22));
  AND_Gate and_10 (.out_3(out_25), .in_1(Data), .in_2(out_24));
  AND_Gate and_11 (.out_3(out_27), .in_1(Data), .in_2(out_26));
  AND_Gate and_12 (.out_3(out_29), .in_1(Data), .in_2(out_28));
  AND_Gate and_13 (.out_3(out_31), .in_1(Data), .in_2(out_30));
  AND_Gate and_14 (.out_3(out_33), .in_1(Data), .in_2(out_32));
  AND_Gate and_15 (.out_3(out_35), .in_1(Data), .in_2(out_34));
  AND_Gate and_16 (.out_3(out_37), .in_1(Data), .in_2(out_36));

  // Notes on the sheet:
  //   A'
  //   B'
  //   C'
  //   D'
endmodule

// Memory
module Memory_Bank (
  input  in_1,
  input  Address,
  input  in_3,
  input  in_4,
  input  in_5,
  input  in_6,
  input  in_7,
  input  in_8,
  input  in_9,
  input  in_10,
  input  in_11,
  input  in_12,
  input  Write,
  output out_14,
  output out_15,
  output out_16,
  output out_17,
  output out_18,
  output out_19,
  output out_20,
  output out_21
);

  wire decoder_demultiplexer_4_16_1_out_6, decoder_demultiplexer_4_16_1_out_7,
       decoder_demultiplexer_4_16_1_out_8, decoder_demultiplexer_4_16_1_out_9,
       decoder_demultiplexer_4_16_1_out_10, decoder_demultiplexer_4_16_1_out_11,
       decoder_demultiplexer_4_16_1_out_12, decoder_demultiplexer_4_16_1_out_13,
       decoder_demultiplexer_4_16_1_out_14, decoder_demultiplexer_4_16_1_out_15,
       decoder_demultiplexer_4_16_1_out_16, decoder_demultiplexer_4_16_1_out_17,
       decoder_demultiplexer_4_16_1_out_18, decoder_demultiplexer_4_16_1_out_19,
       decoder_demultiplexer_4_16_1_out_20, decoder_demultiplexer_4_16_1_out_21,
       decoder_demultiplexer_4_16_1_out_22, decoder_demultiplexer_4_16_1_out_23,
       decoder_demultiplexer_4_16_1_out_24, decoder_demultiplexer_4_16_1_out_25,
       decoder_demultiplexer_4_16_1_out_26, decoder_demultiplexer_4_16_1_out_27,
       decoder_demultiplexer_4_16_1_out_28, decoder_demultiplexer_4_16_1_out_29,
       decoder_demultiplexer_4_16_1_out_30, decoder_demultiplexer_4_16_1_out_31,
       decoder_demultiplexer_4_16_1_out_32, decoder_demultiplexer_4_16_1_out_33,
       decoder_demultiplexer_4_16_1_out_34, decoder_demultiplexer_4_16_1_out_35,
       decoder_demultiplexer_4_16_1_out_36, decoder_demultiplexer_4_16_1_out_37, mux_4_1_out_37,
       mux_4_1_out_38, mux_4_1_out_39, mux_4_1_out_40, mux_4_1_out_41, mux_4_1_out_42, mux_4_1_out_43,
       mux_4_1_out_44, mux_4_2_out_37, mux_4_2_out_38, mux_4_2_out_39, mux_4_2_out_40, mux_4_2_out_41,
       mux_4_2_out_42, mux_4_2_out_43, mux_4_2_out_44, mux_4_3_out_37, mux_4_3_out_38, mux_4_3_out_39,
       mux_4_3_out_40, mux_4_3_out_41, mux_4_3_out_42, mux_4_3_out_43, mux_4_3_out_44, mux_4_4_out_37,
       mux_4_4_out_38, mux_4_4_out_39, mux_4_4_out_40, mux_4_4_out_41, mux_4_4_out_42, mux_4_4_out_43,
       mux_4_4_out_44, Word_2_out_10, Word_2_out_11, Word_2_out_12, Word_2_out_13, Word_2_out_14,
       Word_2_out_15, Word_2_out_16, Word_2_out_17, Word_3_out_10, Word_3_out_11, Word_3_out_12,
       Word_3_out_13, Word_3_out_14, Word_3_out_15, Word_3_out_16, Word_3_out_17, Word_4_out_10,
       Word_4_out_11, Word_4_out_12, Word_4_out_13, Word_4_out_14, Word_4_out_15, Word_4_out_16,
       Word_4_out_17, Word_5_out_10, Word_5_out_11, Word_5_out_12, Word_5_out_13, Word_5_out_14,
       Word_5_out_15, Word_5_out_16, Word_5_out_17, Word_6_out_10, Word_6_out_11, Word_6_out_12,
       Word_6_out_13, Word_6_out_14, Word_6_out_15, Word_6_out_16, Word_6_out_17, Word_7_out_10,
       Word_7_out_11, Word_7_out_12, Word_7_out_13, Word_7_out_14, Word_7_out_15, Word_7_out_16,
       Word_7_out_17, Word_8_out_10, Word_8_out_11, Word_8_out_12, Word_8_out_13, Word_8_out_14,
       Word_8_out_15, Word_8_out_16, Word_8_out_17, Word_9_out_10, Word_9_out_11, Word_9_out_12,
       Word_9_out_13, Word_9_out_14, Word_9_out_15, Word_9_out_16, Word_9_out_17, Word_10_out_10,
       Word_10_out_11, Word_10_out_12, Word_10_out_13, Word_10_out_14, Word_10_out_15, Word_10_out_16,
       Word_10_out_17, Word_11_out_10, Word_11_out_11, Word_11_out_12, Word_11_out_13, Word_11_out_14,
       Word_11_out_15, Word_11_out_16, Word_11_out_17, Word_12_out_10, Word_12_out_11, Word_12_out_12,
       Word_12_out_13, Word_12_out_14, Word_12_out_15, Word_12_out_16, Word_12_out_17, Word_13_out_10,
       Word_13_out_11, Word_13_out_12, Word_13_out_13, Word_13_out_14, Word_13_out_15, Word_13_out_16,
       Word_13_out_17, Word_14_out_10, Word_14_out_11, Word_14_out_12, Word_14_out_13, Word_14_out_14,
       Word_14_out_15, Word_14_out_16, Word_14_out_17, Word_15_out_10, Word_15_out_11, Word_15_out_12,
       Word_15_out_13, Word_15_out_14, Word_15_out_15, Word_15_out_16, Word_15_out_17, Word_16_out_10,
       Word_16_out_11, Word_16_out_12, Word_16_out_13, Word_16_out_14, Word_16_out_15, Word_16_out_16,
       Word_16_out_17, Word_out_10, Word_out_11, Word_out_12, Word_out_13, Word_out_14, Word_out_15,
       Word_out_16, Word_out_17;

  Decoder__Demultiplexer_4_16 decoder_demultiplexer_4_16_1 (
    .out_6(decoder_demultiplexer_4_16_1_out_6), .out_7(decoder_demultiplexer_4_16_1_out_7),
    .out_8(decoder_demultiplexer_4_16_1_out_8), .out_9(decoder_demultiplexer_4_16_1_out_9),
    .out_10(decoder_demultiplexer_4_16_1_out_10), .out_11(decoder_demultiplexer_4_16_1_out_11),
    .out_12(decoder_demultiplexer_4_16_1_out_12), .out_13(decoder_demultiplexer_4_16_1_out_13),
    .out_14(decoder_demultiplexer_4_16_1_out_14), .out_15(decoder_demultiplexer_4_16_1_out_15),
    .out_16(decoder_demultiplexer_4_16_1_out_16), .out_17(decoder_demultiplexer_4_16_1_out_17),
    .out_18(decoder_demultiplexer_4_16_1_out_18), .out_19(decoder_demultiplexer_4_16_1_out_19),
    .out_20(decoder_demultiplexer_4_16_1_out_20), .out_21(decoder_demultiplexer_4_16_1_out_21),
    .out_22(decoder_demultiplexer_4_16_1_out_22), .out_23(decoder_demultiplexer_4_16_1_out_23),
    .out_24(decoder_demultiplexer_4_16_1_out_24), .out_25(decoder_demultiplexer_4_16_1_out_25),
    .out_26(decoder_demultiplexer_4_16_1_out_26), .out_27(decoder_demultiplexer_4_16_1_out_27),
    .out_28(decoder_demultiplexer_4_16_1_out_28), .out_29(decoder_demultiplexer_4_16_1_out_29),
    .out_30(decoder_demultiplexer_4_16_1_out_30), .out_31(decoder_demultiplexer_4_16_1_out_31),
    .out_32(decoder_demultiplexer_4_16_1_out_32), .out_33(decoder_demultiplexer_4_16_1_out_33),
    .out_34(decoder_demultiplexer_4_16_1_out_34), .out_35(decoder_demultiplexer_4_16_1_out_35),
    .out_36(decoder_demultiplexer_4_16_1_out_36), .out_37(decoder_demultiplexer_4_16_1_out_37), .A(in_1),
    .B(Address), .C(in_11), .D(in_12), .Data(Write));
  Register_8_Bit Word (
    .Write(decoder_demultiplexer_4_16_1_out_7), .in_1(in_3), .in_2(in_4), .in_3(in_5), .in_4(in_6),
    .in_5(in_7), .in_6(in_8), .in_7(in_9), .in_8(in_10), .out_10(Word_out_10), .out_11(Word_out_11),
    .out_12(Word_out_12), .out_13(Word_out_13), .out_14(Word_out_14), .out_15(Word_out_15),
    .out_16(Word_out_16), .out_17(Word_out_17));
  Register_8_Bit Word_2 (
    .Write(decoder_demultiplexer_4_16_1_out_23), .in_1(in_3), .in_2(in_4), .in_3(in_5), .in_4(in_6),
    .in_5(in_7), .in_6(in_8), .in_7(in_9), .in_8(in_10), .out_10(Word_2_out_10), .out_11(Word_2_out_11),
    .out_12(Word_2_out_12), .out_13(Word_2_out_13), .out_14(Word_2_out_14), .out_15(Word_2_out_15),
    .out_16(Word_2_out_16), .out_17(Word_2_out_17));
  Register_8_Bit Word_3 (
    .Write(decoder_demultiplexer_4_16_1_out_9), .in_1(in_3), .in_2(in_4), .in_3(in_5), .in_4(in_6),
    .in_5(in_7), .in_6(in_8), .in_7(in_9), .in_8(in_10), .out_10(Word_3_out_10), .out_11(Word_3_out_11),
    .out_12(Word_3_out_12), .out_13(Word_3_out_13), .out_14(Word_3_out_14), .out_15(Word_3_out_15),
    .out_16(Word_3_out_16), .out_17(Word_3_out_17));
  Register_8_Bit Word_4 (
    .Write(decoder_demultiplexer_4_16_1_out_25), .in_1(in_3), .in_2(in_4), .in_3(in_5), .in_4(in_6),
    .in_5(in_7), .in_6(in_8), .in_7(in_9), .in_8(in_10), .out_10(Word_4_out_10), .out_11(Word_4_out_11),
    .out_12(Word_4_out_12), .out_13(Word_4_out_13), .out_14(Word_4_out_14), .out_15(Word_4_out_15),
    .out_16(Word_4_out_16), .out_17(Word_4_out_17));
  Register_8_Bit Word_5 (
    .Write(decoder_demultiplexer_4_16_1_out_11), .in_1(in_3), .in_2(in_4), .in_3(in_5), .in_4(in_6),
    .in_5(in_7), .in_6(in_8), .in_7(in_9), .in_8(in_10), .out_10(Word_5_out_10), .out_11(Word_5_out_11),
    .out_12(Word_5_out_12), .out_13(Word_5_out_13), .out_14(Word_5_out_14), .out_15(Word_5_out_15),
    .out_16(Word_5_out_16), .out_17(Word_5_out_17));
  Mux___4 mux_4_1 (
    .in_9(decoder_demultiplexer_4_16_1_out_6), .in_18(decoder_demultiplexer_4_16_1_out_8),
    .in_27(decoder_demultiplexer_4_16_1_out_10), .in_10(Word_3_out_10), .in_11(Word_3_out_11),
    .in_12(Word_3_out_12), .in_13(Word_3_out_13), .in_14(Word_3_out_14), .in_15(Word_3_out_15),
    .in_16(Word_3_out_16), .in_17(Word_3_out_17), .in_1(Word_out_10), .in_2(Word_out_11), .in_3(Word_out_12),
    .in_4(Word_out_13), .in_5(Word_out_14), .in_6(Word_out_15), .in_7(Word_out_16), .in_8(Word_out_17),
    .in_19(Word_5_out_10), .in_28(Word_7_out_10), .in_20(Word_5_out_11), .in_29(Word_7_out_11),
    .in_21(Word_5_out_12), .in_30(Word_7_out_12), .in_22(Word_5_out_13), .in_31(Word_7_out_13),
    .in_23(Word_5_out_14), .in_32(Word_7_out_14), .in_24(Word_5_out_15), .in_33(Word_7_out_15),
    .in_25(Word_5_out_16), .in_34(Word_7_out_16), .in_26(Word_5_out_17), .in_35(Word_7_out_17),
    .out_37(mux_4_1_out_37), .out_38(mux_4_1_out_38), .out_39(mux_4_1_out_39), .out_40(mux_4_1_out_40),
    .out_41(mux_4_1_out_41), .out_42(mux_4_1_out_42), .out_43(mux_4_1_out_43), .out_44(mux_4_1_out_44),
    .in_36(decoder_demultiplexer_4_16_1_out_12));
  Register_8_Bit Word_6 (
    .Write(decoder_demultiplexer_4_16_1_out_27), .in_1(in_3), .in_2(in_4), .in_3(in_5), .in_4(in_6),
    .in_5(in_7), .in_6(in_8), .in_7(in_9), .in_8(in_10), .out_10(Word_6_out_10), .out_11(Word_6_out_11),
    .out_12(Word_6_out_12), .out_13(Word_6_out_13), .out_14(Word_6_out_14), .out_15(Word_6_out_15),
    .out_16(Word_6_out_16), .out_17(Word_6_out_17));
  Mux___4 mux_4_2 (
    .in_9(decoder_demultiplexer_4_16_1_out_22), .in_18(decoder_demultiplexer_4_16_1_out_24),
    .in_27(decoder_demultiplexer_4_16_1_out_26), .in_10(Word_4_out_10), .in_11(Word_4_out_11),
    .in_12(Word_4_out_12), .in_13(Word_4_out_13), .in_14(Word_4_out_14), .in_15(Word_4_out_15),
    .in_16(Word_4_out_16), .in_17(Word_4_out_17), .in_1(Word_2_out_10), .in_2(Word_2_out_11),
    .in_3(Word_2_out_12), .in_4(Word_2_out_13), .in_5(Word_2_out_14), .in_6(Word_2_out_15),
    .in_7(Word_2_out_16), .in_8(Word_2_out_17), .in_19(Word_6_out_10), .in_28(Word_8_out_10),
    .in_20(Word_6_out_11), .in_29(Word_8_out_11), .in_21(Word_6_out_12), .in_30(Word_8_out_12),
    .in_22(Word_6_out_13), .in_31(Word_8_out_13), .in_23(Word_6_out_14), .in_32(Word_8_out_14),
    .in_24(Word_6_out_15), .in_33(Word_8_out_15), .in_25(Word_6_out_16), .in_34(Word_8_out_16),
    .in_26(Word_6_out_17), .in_35(Word_8_out_17), .out_37(mux_4_2_out_37), .out_38(mux_4_2_out_38),
    .out_39(mux_4_2_out_39), .out_40(mux_4_2_out_40), .out_41(mux_4_2_out_41), .out_42(mux_4_2_out_42),
    .out_43(mux_4_2_out_43), .out_44(mux_4_2_out_44), .in_36(decoder_demultiplexer_4_16_1_out_28));
  Register_8_Bit Word_7 (
    .Write(decoder_demultiplexer_4_16_1_out_13), .in_1(in_3), .in_2(in_4), .in_3(in_5), .in_4(in_6),
    .in_5(in_7), .in_6(in_8), .in_7(in_9), .in_8(in_10), .out_10(Word_7_out_10), .out_11(Word_7_out_11),
    .out_12(Word_7_out_12), .out_13(Word_7_out_13), .out_14(Word_7_out_14), .out_15(Word_7_out_15),
    .out_16(Word_7_out_16), .out_17(Word_7_out_17));
  Register_8_Bit Word_8 (
    .Write(decoder_demultiplexer_4_16_1_out_29), .in_1(in_3), .in_2(in_4), .in_3(in_5), .in_4(in_6),
    .in_5(in_7), .in_6(in_8), .in_7(in_9), .in_8(in_10), .out_10(Word_8_out_10), .out_11(Word_8_out_11),
    .out_12(Word_8_out_12), .out_13(Word_8_out_13), .out_14(Word_8_out_14), .out_15(Word_8_out_15),
    .out_16(Word_8_out_16), .out_17(Word_8_out_17));
  Register_8_Bit Word_9 (
    .Write(decoder_demultiplexer_4_16_1_out_15), .in_1(in_3), .in_2(in_4), .in_3(in_5), .in_4(in_6),
    .in_5(in_7), .in_6(in_8), .in_7(in_9), .in_8(in_10), .out_10(Word_9_out_10), .out_11(Word_9_out_11),
    .out_12(Word_9_out_12), .out_13(Word_9_out_13), .out_14(Word_9_out_14), .out_15(Word_9_out_15),
    .out_16(Word_9_out_16), .out_17(Word_9_out_17));
  Register_8_Bit Word_10 (
    .Write(decoder_demultiplexer_4_16_1_out_31), .in_1(in_3), .in_2(in_4), .in_3(in_5), .in_4(in_6),
    .in_5(in_7), .in_6(in_8), .in_7(in_9), .in_8(in_10), .out_10(Word_10_out_10), .out_11(Word_10_out_11),
    .out_12(Word_10_out_12), .out_13(Word_10_out_13), .out_14(Word_10_out_14), .out_15(Word_10_out_15),
    .out_16(Word_10_out_16), .out_17(Word_10_out_17));
  Register_8_Bit Word_11 (
    .Write(decoder_demultiplexer_4_16_1_out_17), .in_1(in_3), .in_2(in_4), .in_3(in_5), .in_4(in_6),
    .in_5(in_7), .in_6(in_8), .in_7(in_9), .in_8(in_10), .out_10(Word_11_out_10), .out_11(Word_11_out_11),
    .out_12(Word_11_out_12), .out_13(Word_11_out_13), .out_14(Word_11_out_14), .out_15(Word_11_out_15),
    .out_16(Word_11_out_16), .out_17(Word_11_out_17));
  Register_8_Bit Word_12 (
    .Write(decoder_demultiplexer_4_16_1_out_33), .in_1(in_3), .in_2(in_4), .in_3(in_5), .in_4(in_6),
    .in_5(in_7), .in_6(in_8), .in_7(in_9), .in_8(in_10), .out_10(Word_12_out_10), .out_11(Word_12_out_11),
    .out_12(Word_12_out_12), .out_13(Word_12_out_13), .out_14(Word_12_out_14), .out_15(Word_12_out_15),
    .out_16(Word_12_out_16), .out_17(Word_12_out_17));
  Register_8_Bit Word_13 (
    .Write(decoder_demultiplexer_4_16_1_out_19), .in_1(in_3), .in_2(in_4), .in_3(in_5), .in_4(in_6),
    .in_5(in_7), .in_6(in_8), .in_7(in_9), .in_8(in_10), .out_10(Word_13_out_10), .out_11(Word_13_out_11),
    .out_12(Word_13_out_12), .out_13(Word_13_out_13), .out_14(Word_13_out_14), .out_15(Word_13_out_15),
    .out_16(Word_13_out_16), .out_17(Word_13_out_17));
  Mux___4 mux_4_3 (
    .in_9(decoder_demultiplexer_4_16_1_out_14), .in_18(decoder_demultiplexer_4_16_1_out_16),
    .in_27(decoder_demultiplexer_4_16_1_out_18), .in_10(Word_11_out_10), .in_11(Word_11_out_11),
    .in_12(Word_11_out_12), .in_13(Word_11_out_13), .in_14(Word_11_out_14), .in_15(Word_11_out_15),
    .in_16(Word_11_out_16), .in_17(Word_11_out_17), .in_1(Word_9_out_10), .in_2(Word_9_out_11),
    .in_3(Word_9_out_12), .in_4(Word_9_out_13), .in_5(Word_9_out_14), .in_6(Word_9_out_15),
    .in_7(Word_9_out_16), .in_8(Word_9_out_17), .in_19(Word_13_out_10), .in_28(Word_15_out_10),
    .in_20(Word_13_out_11), .in_29(Word_15_out_11), .in_21(Word_13_out_12), .in_30(Word_15_out_12),
    .in_22(Word_13_out_13), .in_31(Word_15_out_13), .in_23(Word_13_out_14), .in_32(Word_15_out_14),
    .in_24(Word_13_out_15), .in_33(Word_15_out_15), .in_25(Word_13_out_16), .in_34(Word_15_out_16),
    .in_26(Word_13_out_17), .in_35(Word_15_out_17), .out_37(mux_4_3_out_37), .out_38(mux_4_3_out_38),
    .out_39(mux_4_3_out_39), .out_40(mux_4_3_out_40), .out_41(mux_4_3_out_41), .out_42(mux_4_3_out_42),
    .out_43(mux_4_3_out_43), .out_44(mux_4_3_out_44), .in_36(decoder_demultiplexer_4_16_1_out_20));
  Register_8_Bit Word_14 (
    .Write(decoder_demultiplexer_4_16_1_out_35), .in_1(in_3), .in_2(in_4), .in_3(in_5), .in_4(in_6),
    .in_5(in_7), .in_6(in_8), .in_7(in_9), .in_8(in_10), .out_10(Word_14_out_10), .out_11(Word_14_out_11),
    .out_12(Word_14_out_12), .out_13(Word_14_out_13), .out_14(Word_14_out_14), .out_15(Word_14_out_15),
    .out_16(Word_14_out_16), .out_17(Word_14_out_17));
  Mux___4 mux_4_4 (
    .in_9(decoder_demultiplexer_4_16_1_out_30), .in_18(decoder_demultiplexer_4_16_1_out_32),
    .in_27(decoder_demultiplexer_4_16_1_out_34), .in_10(Word_12_out_10), .in_11(Word_12_out_11),
    .in_12(Word_12_out_12), .in_13(Word_12_out_13), .in_14(Word_12_out_14), .in_15(Word_12_out_15),
    .in_16(Word_12_out_16), .in_17(Word_12_out_17), .in_1(Word_10_out_10), .in_2(Word_10_out_11),
    .in_3(Word_10_out_12), .in_4(Word_10_out_13), .in_5(Word_10_out_14), .in_6(Word_10_out_15),
    .in_7(Word_10_out_16), .in_8(Word_10_out_17), .in_19(Word_14_out_10), .in_28(Word_16_out_10),
    .in_20(Word_14_out_11), .in_29(Word_16_out_11), .in_21(Word_14_out_12), .in_30(Word_16_out_12),
    .in_22(Word_14_out_13), .in_31(Word_16_out_13), .in_23(Word_14_out_14), .in_32(Word_16_out_14),
    .in_24(Word_14_out_15), .in_33(Word_16_out_15), .in_25(Word_14_out_16), .in_34(Word_16_out_16),
    .in_26(Word_14_out_17), .in_35(Word_16_out_17), .out_37(mux_4_4_out_37), .out_38(mux_4_4_out_38),
    .out_39(mux_4_4_out_39), .out_40(mux_4_4_out_40), .out_41(mux_4_4_out_41), .out_42(mux_4_4_out_42),
    .out_43(mux_4_4_out_43), .out_44(mux_4_4_out_44), .in_36(decoder_demultiplexer_4_16_1_out_36));
  Register_8_Bit Word_15 (
    .Write(decoder_demultiplexer_4_16_1_out_21), .in_1(in_3), .in_2(in_4), .in_3(in_5), .in_4(in_6),
    .in_5(in_7), .in_6(in_8), .in_7(in_9), .in_8(in_10), .out_10(Word_15_out_10), .out_11(Word_15_out_11),
    .out_12(Word_15_out_12), .out_13(Word_15_out_13), .out_14(Word_15_out_14), .out_15(Word_15_out_15),
    .out_16(Word_15_out_16), .out_17(Word_15_out_17));
  Register_8_Bit Word_16 (
    .Write(decoder_demultiplexer_4_16_1_out_37), .in_1(in_3), .in_2(in_4), .in_3(in_5), .in_4(in_6),
    .in_5(in_7), .in_6(in_8), .in_7(in_9), .in_8(in_10), .out_10(Word_16_out_10), .out_11(Word_16_out_11),
    .out_12(Word_16_out_12), .out_13(Word_16_out_13), .out_14(Word_16_out_14), .out_15(Word_16_out_15),
    .out_16(Word_16_out_16), .out_17(Word_16_out_17));
  Mux___4 mux_4_5 (
    .in_9(1'b1), .in_18(1'b1), .in_27(1'b1), .in_10(mux_4_4_out_37), .in_11(mux_4_4_out_38),
    .in_12(mux_4_4_out_39), .in_13(mux_4_4_out_40), .in_14(mux_4_4_out_41), .in_15(mux_4_4_out_42),
    .in_16(mux_4_4_out_43), .in_17(mux_4_4_out_44), .in_1(mux_4_2_out_37), .in_2(mux_4_2_out_38),
    .in_3(mux_4_2_out_39), .in_4(mux_4_2_out_40), .in_5(mux_4_2_out_41), .in_6(mux_4_2_out_42),
    .in_7(mux_4_2_out_43), .in_8(mux_4_2_out_44), .in_19(mux_4_1_out_37), .in_28(mux_4_3_out_37),
    .in_20(mux_4_1_out_38), .in_29(mux_4_3_out_38), .in_21(mux_4_1_out_39), .in_30(mux_4_3_out_39),
    .in_22(mux_4_1_out_40), .in_31(mux_4_3_out_40), .in_23(mux_4_1_out_41), .in_32(mux_4_3_out_41),
    .in_24(mux_4_1_out_42), .in_33(mux_4_3_out_42), .in_25(mux_4_1_out_43), .in_34(mux_4_3_out_43),
    .in_26(mux_4_1_out_44), .in_35(mux_4_3_out_44), .out_37(out_14), .out_38(out_15), .out_39(out_16),
    .out_40(out_17), .out_41(out_18), .out_42(out_19), .out_43(out_20), .out_44(out_21), .in_36(1'b1));
endmodule

module circuit_2_2_2 (
);


  // Notes on the sheet:
  //   it gets better
endmodule
module Incrementer_4_bit (
  input  in_1,
  input  in_2,
  input  in_3,
  input  in_4,
  output out_5,
  output out_6,
  output out_7,
  output out_8
);

  wire and_2_out_3, and_3_out_3, and_4_out_3;

  AND_Gate and_1 (.in_1(in_1), .in_2(and_2_out_3));  // open: out_3
  XOR_Gate xor_1 (.in_1(and_2_out_3), .in_2(in_1), .out_3(out_5));
  AND_Gate and_2 (.out_3(and_2_out_3), .in_1(in_2), .in_2(and_3_out_3));
  XOR_Gate xor_2 (.in_1(and_3_out_3), .in_2(in_2), .out_3(out_6));
  AND_Gate and_3 (.out_3(and_3_out_3), .in_1(in_3), .in_2(and_4_out_3));
  XOR_Gate xor_3 (.in_1(and_4_out_3), .in_2(in_3), .out_3(out_7));
  AND_Gate and_4 (.out_3(and_4_out_3), .in_1(in_4), .in_2(1'b1));
  XOR_Gate xor_4 (.in_1(1'b1), .in_2(in_4), .out_3(out_8));
endmodule

// Mux
module Mux__PC (
  input  in_1,
  input  in_2,
  input  in_3,
  input  in_4,
  input  in_5,
  input  in_6,
  input  in_7,
  input  in_8,
  input  in_9,
  input  in_10,
  input  in_11,
  input  in_12,
  input  in_13,
  input  in_14,
  input  in_15,
  input  in_16,
  input  in_17,
  input  in_18,
  output out_19,
  output out_20,
  output out_21,
  output out_22,
  output out_23,
  output out_24,
  output out_25,
  output out_26
);

  wire flow_control_1_out_10, flow_control_1_out_11, flow_control_1_out_12, flow_control_1_out_13,
       flow_control_1_out_14, flow_control_1_out_15, flow_control_1_out_16, flow_control_1_out_17,
       flow_control_2_out_10, flow_control_2_out_11, flow_control_2_out_12, flow_control_2_out_13,
       flow_control_2_out_14, flow_control_2_out_15, flow_control_2_out_16, flow_control_2_out_17;

  Flow_Control flow_control_1 (
    .in_9(in_18), .in_1(in_10), .in_2(in_11), .in_3(in_12), .in_4(in_13), .in_5(in_14), .in_6(in_15),
    .in_7(in_16), .in_8(in_17), .out_10(flow_control_1_out_10), .out_11(flow_control_1_out_11),
    .out_12(flow_control_1_out_12), .out_13(flow_control_1_out_13), .out_14(flow_control_1_out_14),
    .out_15(flow_control_1_out_15), .out_16(flow_control_1_out_16), .out_17(flow_control_1_out_17));
  Flow_Control flow_control_2 (
    .in_9(in_9), .in_1(in_1), .in_2(in_2), .in_3(in_3), .in_4(in_4), .in_5(in_5), .in_6(in_6), .in_7(in_7),
    .in_8(in_8), .out_10(flow_control_2_out_10), .out_11(flow_control_2_out_11),
    .out_12(flow_control_2_out_12), .out_13(flow_control_2_out_13), .out_14(flow_control_2_out_14),
    .out_15(flow_control_2_out_15), .out_16(flow_control_2_out_16), .out_17(flow_control_2_out_17));
  _3_Input_1_Output u_3_input_1_output_1 (
    .in_1(flow_control_1_out_10), .in_2(flow_control_1_out_11), .in_3(flow_control_1_out_12),
    .in_4(flow_control_1_out_13), .in_5(flow_control_1_out_14), .in_6(flow_control_1_out_15),
    .in_7(flow_control_1_out_16), .in_8(flow_control_1_out_17), .in_9(flow_control_2_out_10),
    .in_10(flow_control_2_out_11), .in_11(flow_control_2_out_12), .in_12(flow_control_2_out_13),
    .in_13(flow_control_2_out_14), .in_14(flow_control_2_out_15), .in_15(flow_control_2_out_16),
    .in_16(flow_control_2_out_17), .in_17(1'b0), .in_18(1'b0), .in_19(1'b0), .in_20(1'b0), .in_21(1'b0),
    .in_22(1'b0), .in_23(1'b0), .out_25(out_19), .out_26(out_20), .out_27(out_21), .out_28(out_22),
    .out_29(out_23), .out_30(out_24), .out_31(out_25), .in_24(1'b0), .out_32(out_26));
endmodule

module PC (
  input  Step,
  input  in_2,
  input  in_3,
  input  in_4,
  input  in_5,
  input  Load,
  input  Increment,
  input  Write,
  output out_9,
  output out_10,
  output out_11,
  output out_12
);

  wire Incrementer_out_5, Incrementer_out_6, Incrementer_out_7, Incrementer_out_8, mux_pc_1_out_19,
       mux_pc_1_out_20, mux_pc_1_out_21, mux_pc_1_out_22, mux_pc_1_out_23, or_1_out_3, or_2_out_3;

  OR_Gate or_1 (.out_3(or_1_out_3), .in_1(Step), .in_2(Increment));
  OR_Gate or_2 (.out_3(or_2_out_3), .in_1(Step), .in_2(Write));
  Register_4_Bit register_4_bit_1 (
    .Write(or_2_out_3), .in_1(mux_pc_1_out_19), .in_2(mux_pc_1_out_20), .in_3(mux_pc_1_out_21),
    .in_4(mux_pc_1_out_22), .out_6(out_9), .out_7(out_10), .out_8(out_11), .out_9(out_12));
  Incrementer_4_bit Incrementer (
    .in_1(out_9), .in_2(out_10), .in_3(out_11), .in_4(out_12), .out_5(Incrementer_out_5),
    .out_6(Incrementer_out_6), .out_7(Incrementer_out_7), .out_8(Incrementer_out_8));
  Mux__PC mux_pc_1 (
    .in_18(Load), .out_22(mux_pc_1_out_22), .out_21(mux_pc_1_out_21), .out_19(mux_pc_1_out_19),
    .out_20(mux_pc_1_out_20), .in_14(1'b0), .in_15(1'b0), .in_16(1'b0), .in_17(1'b0), .in_10(in_2),
    .in_11(in_3), .in_12(in_4), .in_13(in_5), .in_1(Incrementer_out_5), .in_2(Incrementer_out_6),
    .in_3(Incrementer_out_7), .in_4(Incrementer_out_8), .in_5(1'b0), .in_6(1'b0), .in_7(1'b0), .in_8(1'b0),
    .in_9(or_1_out_3), .out_23(mux_pc_1_out_23), .out_24(mux_pc_1_out_23), .out_25(mux_pc_1_out_23),
    .out_26(mux_pc_1_out_23));
  // also tied to GND on the sheet: mux_pc_1_out_23
endmodule

module circuit_2_2_2_2 (
);


  // Notes on the sheet:
  //   teamwork makes the dreamwork
endmodule

// NOT
module _8_Bit_NOT (
  input  in_1,
  input  in_2,
  input  in_3,
  input  in_4,
  input  in_5,
  input  in_6,
  input  in_7,
  input  in_8,
  output out_9,
  output out_10,
  output out_11,
  output out_12,
  output out_13,
  output out_14,
  output out_15,
  output out_16
);

  NOT_Gate not_1 (.out_2(out_9), .in_1(in_1));
  NOT_Gate not_2 (.out_2(out_10), .in_1(in_2));
  NOT_Gate not_3 (.out_2(out_12), .in_1(in_4));
  NOT_Gate not_4 (.out_2(out_11), .in_1(in_3));
  NOT_Gate not_5 (.out_2(out_13), .in_1(in_5));
  NOT_Gate not_6 (.out_2(out_14), .in_1(in_6));
  NOT_Gate not_7 (.out_2(out_15), .in_1(in_7));
  NOT_Gate not_8 (.out_2(out_16), .in_1(in_8));
endmodule

// Control
module Control_Unit (
  input  Fetch,
  input  Fetch_Write,
  input  Execute,
  input  Execute_Write,
  input  in_5,
  input  Opcode,
  input  in_7,
  input  in_8,
  input  in_9,
  input  in_10,
  input  R,
  input  in_12,
  input  in_13,
  input  in_14,
  input  in_15,
  input  in_16,
  output No_Shift,
  output Left_Shift,
  output Halt,
  output Right_Shift,
  output ALU_ADD,
  output ALU_AND,
  output ALU_XOR,
  output Memory_Write,
  output R_MUX_ALU,
  output R_MUX_Memory,
  output R_MUX_IR,
  output R_Write,
  output PC_Load,
  output PC_Increment,
  output PC_Write,
  output ADDR_Mux_PC,
  output IR_Write,
  output ADDR_Mux_IR
);

  wire and_5_1_out_6, and_5_7_out_6, and_5_8_out_6, and_5_10_out_6, and_5_11_out_6, and_5_12_out_6,
       and_5_13_out_6, and_5_14_out_6, and_5_16_out_6, n8_bit_not_1_out_9, n8_bit_not_1_out_10,
       n8_bit_not_1_out_11, n8_bit_not_1_out_12, n8_bit_not_1_out_13, n8_bit_not_1_out_14,
       n8_bit_not_1_out_15, n8_bit_not_1_out_16, not_1_out_2, not_2_out_2, not_3_out_2, not_4_out_2,
       not_5_out_2, not_6_out_2, not_7_out_2, not_8_out_2;

  NOR_Gate nor_1 (.out_3(No_Shift), .in_1(1'b0), .in_2(1'b0));
  OR_Gate___5 or_5_1 (.out_6(R_MUX_ALU), .in_1(ALU_XOR), .in_2(1'b0), .in_3(ALU_AND), .in_4(1'b0), .in_5(ALU_ADD));
  _8_Bit_NOT u_8_bit_not_1 (
    .in_1(in_9), .in_2(in_10), .in_3(R), .in_4(in_12), .in_5(in_13), .in_6(in_14), .in_7(in_15),
    .in_8(in_16), .out_9(n8_bit_not_1_out_9), .out_10(n8_bit_not_1_out_10), .out_11(n8_bit_not_1_out_11),
    .out_12(n8_bit_not_1_out_12), .out_13(n8_bit_not_1_out_13), .out_14(n8_bit_not_1_out_14),
    .out_15(n8_bit_not_1_out_15), .out_16(n8_bit_not_1_out_16));
  AND_Gate___5 and_5_1 (
    .in_1(not_2_out_2), .in_2(not_3_out_2), .in_3(not_4_out_2), .in_4(not_1_out_2), .in_5(Execute),
    .out_6(and_5_1_out_6));
  AND_Gate___5 and_5_2 (
    .in_1(not_2_out_2), .in_2(not_3_out_2), .in_3(in_7), .in_4(not_1_out_2), .in_5(Execute), .out_6(ALU_ADD));
  AND_Gate___5 and_5_3 (
    .in_1(not_2_out_2), .in_2(Opcode), .in_3(not_4_out_2), .in_4(not_1_out_2), .in_5(Execute), .out_6(ALU_AND));
  AND_Gate___5 and_5_4 (
    .in_1(not_2_out_2), .in_2(Opcode), .in_3(in_7), .in_4(not_1_out_2), .in_5(Execute), .out_6(ALU_XOR));
  AND_Gate___5 and_5_5 (
    .in_1(in_5), .in_2(not_3_out_2), .in_3(not_4_out_2), .in_4(not_1_out_2), .in_5(Execute), .out_6(R_MUX_IR));
  AND_Gate___5 and_5_6 (
    .in_1(in_5), .in_2(not_3_out_2), .in_3(in_7), .in_4(not_1_out_2), .in_5(Execute), .out_6(R_MUX_Memory));
  AND_Gate___5 and_5_7 (
    .in_1(in_5), .in_2(Opcode), .in_3(not_4_out_2), .in_4(not_1_out_2), .in_5(Execute), .out_6(and_5_7_out_6));
  AND_Gate___5 and_5_8 (
    .in_1(in_5), .in_2(Opcode), .in_3(in_7), .in_4(not_1_out_2), .in_5(Execute), .out_6(and_5_8_out_6));
  AND_Gate___9 and_9_1 (
    .in_1(n8_bit_not_1_out_9), .in_2(n8_bit_not_1_out_10), .in_3(n8_bit_not_1_out_11),
    .in_4(n8_bit_not_1_out_12), .in_5(n8_bit_not_1_out_13), .in_6(n8_bit_not_1_out_14),
    .in_7(n8_bit_not_1_out_15), .in_8(n8_bit_not_1_out_16), .in_9(and_5_8_out_6), .out_10(PC_Load));
  NOT_Gate not_1 (.out_2(not_1_out_2), .in_1(in_8));
  NOT_Gate not_2 (.out_2(not_2_out_2), .in_1(in_5));
  NOT_Gate not_3 (.out_2(not_3_out_2), .in_1(Opcode));
  NOT_Gate not_4 (.out_2(not_4_out_2), .in_1(in_7));
  NOT_Gate not_5 (.out_2(not_5_out_2), .in_1(in_7));
  NOT_Gate not_6 (.out_2(not_6_out_2), .in_1(in_8));
  NOT_Gate not_7 (.out_2(not_7_out_2), .in_1(in_5));
  NOT_Gate not_8 (.out_2(not_8_out_2), .in_1(Opcode));
  AND_Gate___5 and_5_9 (
    .in_1(Execute_Write), .in_2(not_6_out_2), .in_3(not_5_out_2), .in_4(not_8_out_2), .in_5(not_7_out_2),
    .out_6(Halt));
  AND_Gate___5 and_5_10 (
    .in_1(Execute_Write), .in_2(not_6_out_2), .in_3(in_7), .in_4(not_8_out_2), .in_5(not_7_out_2),
    .out_6(and_5_10_out_6));
  AND_Gate___5 and_5_11 (
    .in_1(Execute_Write), .in_2(not_6_out_2), .in_3(not_5_out_2), .in_4(Opcode), .in_5(not_7_out_2),
    .out_6(and_5_11_out_6));
  AND_Gate___5 and_5_12 (
    .in_1(Execute_Write), .in_2(not_6_out_2), .in_3(in_7), .in_4(Opcode), .in_5(not_7_out_2),
    .out_6(and_5_12_out_6));
  AND_Gate___5 and_5_13 (
    .in_1(Execute_Write), .in_2(not_6_out_2), .in_3(not_5_out_2), .in_4(not_8_out_2), .in_5(in_5),
    .out_6(and_5_13_out_6));
  AND_Gate___5 and_5_14 (
    .in_1(Execute_Write), .in_2(not_6_out_2), .in_3(in_7), .in_4(not_8_out_2), .in_5(in_5),
    .out_6(and_5_14_out_6));
  AND_Gate___5 and_5_15 (
    .in_1(Execute_Write), .in_2(not_6_out_2), .in_3(not_5_out_2), .in_4(Opcode), .in_5(in_5),
    .out_6(Memory_Write));
  AND_Gate___5 and_5_16 (
    .in_1(Execute_Write), .in_2(not_6_out_2), .in_3(in_7), .in_4(Opcode), .in_5(in_5), .out_6(and_5_16_out_6));
  OR_Gate___3 or_3_1 (.out_4(ADDR_Mux_IR), .in_1(and_5_7_out_6), .in_2(R_MUX_ALU), .in_3(R_MUX_Memory));
  NOT_Gate not_9 (.out_2(PC_Increment), .in_1(PC_Load));
  OR_Gate___5 or_5_2 (
    .out_6(R_Write), .in_1(and_5_14_out_6), .in_2(and_5_13_out_6), .in_3(and_5_12_out_6),
    .in_4(and_5_11_out_6), .in_5(and_5_10_out_6));

  assign ADDR_Mux_PC = Fetch;
  assign IR_Write = Fetch_Write;
  assign Left_Shift = 1'b0;
  assign PC_Write = Execute_Write;
  assign Right_Shift = 1'b0;
endmodule

// CU
module CU__new (
  input  Fetch,
  input  Fetch_Write,
  input  Opcode,
  input  in_4,
  input  in_5,
  input  in_6,
  input  Execute,
  input  Execute_Write,
  input  in_9,
  input  in_10,
  input  in_11,
  input  R,
  input  in_13,
  input  in_14,
  input  in_15,
  input  in_16,
  output Halt,
  output No_Shift,
  output ADD,
  output Left_Shift,
  output XOR,
  output Right_Shift,
  output AND,
  output R_Write,
  output Subtract,
  output R_MUX_IR,
  output R_MUX_Memory,
  output Memory_Write,
  output Addr_Mux_IR,
  output R_Mux_ALU,
  output ADDR_Mux_PC,
  output PC_Load,
  output PC_Increment,
  output PC_Write,
  output IR_Write
);

  wire decoder_demultiplexer_4_16_1_out_31, decoder_demultiplexer_4_16_1_out_35,
       decoder_demultiplexer_4_16_2_out_11, decoder_demultiplexer_4_16_2_out_13,
       decoder_demultiplexer_4_16_2_out_15, decoder_demultiplexer_4_16_2_out_17,
       decoder_demultiplexer_4_16_2_out_19, decoder_demultiplexer_4_16_2_out_21,
       decoder_demultiplexer_4_16_2_out_23, decoder_demultiplexer_4_16_2_out_27, n8_bit_not_1_out_9,
       n8_bit_not_1_out_10, n8_bit_not_1_out_11, n8_bit_not_1_out_12, n8_bit_not_1_out_13,
       n8_bit_not_1_out_14, n8_bit_not_1_out_15, n8_bit_not_1_out_16;

  Decoder__Demultiplexer_4_16 decoder_demultiplexer_4_16_1 (
    .out_11(ADD), .out_13(Left_Shift), .out_15(XOR), .out_17(Right_Shift), .out_19(AND), .out_21(Subtract),
    .out_23(R_MUX_IR), .out_27(R_MUX_Memory), .out_31(decoder_demultiplexer_4_16_1_out_31),
    .out_35(decoder_demultiplexer_4_16_1_out_35), .A(Opcode), .B(in_4), .C(in_5), .D(in_6), .Data(Execute));  // open: out_6, out_7, out_8, out_9, out_10, out_12, out_14, out_16, out_18, out_20, out_22, out_24, out_25, out_26, out_28, out_29, out_30, out_32, out_33, out_34, out_36, out_37
  _8_Bit_NOT u_8_bit_not_1 (
    .in_1(in_9), .in_2(in_10), .in_3(in_11), .in_4(R), .in_5(in_13), .in_6(in_14), .in_7(in_15),
    .in_8(in_16), .out_9(n8_bit_not_1_out_9), .out_10(n8_bit_not_1_out_10), .out_11(n8_bit_not_1_out_11),
    .out_12(n8_bit_not_1_out_12), .out_13(n8_bit_not_1_out_13), .out_14(n8_bit_not_1_out_14),
    .out_15(n8_bit_not_1_out_15), .out_16(n8_bit_not_1_out_16));
  AND_Gate___9 and_9_1 (
    .in_1(n8_bit_not_1_out_9), .in_2(n8_bit_not_1_out_10), .in_3(n8_bit_not_1_out_11),
    .in_4(n8_bit_not_1_out_12), .in_5(n8_bit_not_1_out_13), .in_6(n8_bit_not_1_out_14),
    .in_7(n8_bit_not_1_out_15), .in_8(n8_bit_not_1_out_16), .in_9(decoder_demultiplexer_4_16_1_out_35),
    .out_10(PC_Load));
  OR_Gate___3 or_3_1 (
    .out_4(Addr_Mux_IR), .in_1(R_Mux_ALU), .in_2(decoder_demultiplexer_4_16_1_out_31), .in_3(R_MUX_Memory));
  NOT_Gate not_1 (.out_2(PC_Increment), .in_1(PC_Load));
  NOR_Gate nor_1 (.out_3(No_Shift), .in_1(Left_Shift), .in_2(Right_Shift));
  // OR_Gate___7 or_7_1: pin names not known; wires that end beside it: R_Mux_ALU
  Decoder__Demultiplexer_4_16 decoder_demultiplexer_4_16_2 (
    .out_7(Halt), .out_11(decoder_demultiplexer_4_16_2_out_11), .out_13(decoder_demultiplexer_4_16_2_out_13),
    .out_15(decoder_demultiplexer_4_16_2_out_15), .out_17(decoder_demultiplexer_4_16_2_out_17),
    .out_19(decoder_demultiplexer_4_16_2_out_19), .out_21(decoder_demultiplexer_4_16_2_out_21),
    .out_23(decoder_demultiplexer_4_16_2_out_23), .out_27(decoder_demultiplexer_4_16_2_out_27),
    .out_31(Memory_Write), .A(Opcode), .B(in_4), .C(in_5), .D(in_6), .Data(Execute_Write));  // open: out_6, out_8, out_9, out_10, out_12, out_14, out_16, out_18, out_20, out_22, out_24, out_25, out_26, out_28, out_29, out_30, out_32, out_33, out_34, out_35, out_36, out_37
  OR_Gate___8 or_8_1 (
    .out_9(R_Write), .in_1(decoder_demultiplexer_4_16_2_out_27), .in_2(decoder_demultiplexer_4_16_2_out_21),
    .in_3(decoder_demultiplexer_4_16_2_out_23), .in_4(decoder_demultiplexer_4_16_2_out_19),
    .in_5(decoder_demultiplexer_4_16_2_out_17), .in_6(decoder_demultiplexer_4_16_2_out_15),
    .in_7(decoder_demultiplexer_4_16_2_out_13), .in_8(decoder_demultiplexer_4_16_2_out_11));

  assign ADDR_Mux_PC = Fetch;
  assign IR_Write = Fetch_Write;
  assign PC_Write = Execute_Write;
endmodule

module circuit_2_2_2_2_2 (
);


  // Notes on the sheet:
  //   soosoeoeoeo tired
endmodule

module R_Mux (
  input  in_1,
  input  in_2,
  input  in_3,
  input  in_4,
  input  in_5,
  input  in_6,
  input  in_7,
  input  in_8,
  input  in_9,
  input  in_10,
  input  in_11,
  input  in_12,
  input  in_13,
  input  in_14,
  input  in_15,
  input  in_16,
  input  in_17,
  input  in_18,
  input  in_19,
  input  in_20,
  input  in_21,
  input  in_22,
  input  in_23,
  input  in_24,
  input  in_25,
  input  in_26,
  input  in_27,
  output out_28,
  output out_29,
  output out_30,
  output out_31,
  output out_32,
  output out_33,
  output out_34,
  output out_35
);

  wire flow_control_1_out_10, flow_control_1_out_11, flow_control_1_out_12, flow_control_1_out_13,
       flow_control_1_out_14, flow_control_1_out_15, flow_control_1_out_16, flow_control_1_out_17,
       flow_control_2_out_10, flow_control_2_out_11, flow_control_2_out_12, flow_control_2_out_13,
       flow_control_2_out_14, flow_control_2_out_15, flow_control_2_out_16, flow_control_2_out_17,
       flow_control_3_out_10, flow_control_3_out_11, flow_control_3_out_12, flow_control_3_out_13,
       flow_control_3_out_14, flow_control_3_out_15, flow_control_3_out_16, flow_control_3_out_17;

  Flow_Control flow_control_1 (
    .in_9(in_18), .in_1(in_10), .in_2(in_11), .in_3(in_12), .in_4(in_13), .in_5(in_14), .in_6(in_15),
    .in_7(in_16), .in_8(in_17), .out_10(flow_control_1_out_10), .out_11(flow_control_1_out_11),
    .out_12(flow_control_1_out_12), .out_13(flow_control_1_out_13), .out_14(flow_control_1_out_14),
    .out_15(flow_control_1_out_15), .out_16(flow_control_1_out_16), .out_17(flow_control_1_out_17));
  Flow_Control flow_control_2 (
    .in_9(in_9), .in_1(in_1), .in_2(in_2), .in_3(in_3), .in_4(in_4), .in_5(in_5), .in_6(in_6), .in_7(in_7),
    .in_8(in_8), .out_10(flow_control_2_out_10), .out_11(flow_control_2_out_11),
    .out_12(flow_control_2_out_12), .out_13(flow_control_2_out_13), .out_14(flow_control_2_out_14),
    .out_15(flow_control_2_out_15), .out_16(flow_control_2_out_16), .out_17(flow_control_2_out_17));
  _3_Input_1_Output u_3_input_1_output_1 (
    .in_1(flow_control_1_out_10), .in_2(flow_control_1_out_11), .in_3(flow_control_1_out_12),
    .in_4(flow_control_1_out_13), .in_5(flow_control_1_out_14), .in_6(flow_control_1_out_15),
    .in_7(flow_control_1_out_16), .in_8(flow_control_1_out_17), .in_9(flow_control_2_out_10),
    .in_10(flow_control_2_out_11), .in_11(flow_control_2_out_12), .in_12(flow_control_2_out_13),
    .in_13(flow_control_2_out_14), .in_14(flow_control_2_out_15), .in_15(flow_control_2_out_16),
    .in_16(flow_control_2_out_17), .in_17(flow_control_3_out_10), .in_18(flow_control_3_out_11),
    .in_19(flow_control_3_out_12), .in_20(flow_control_3_out_13), .in_21(flow_control_3_out_14),
    .in_22(flow_control_3_out_15), .in_23(flow_control_3_out_16), .out_25(out_28), .out_26(out_29),
    .out_27(out_30), .out_28(out_31), .out_29(out_32), .out_30(out_33), .out_31(out_34),
    .in_24(flow_control_3_out_17), .out_32(out_35));
  Flow_Control flow_control_3 (
    .in_9(in_27), .in_1(in_19), .in_2(in_20), .in_3(in_21), .in_4(in_22), .in_5(in_23), .in_6(in_24),
    .in_7(in_25), .in_8(in_26), .out_10(flow_control_3_out_10), .out_11(flow_control_3_out_11),
    .out_12(flow_control_3_out_12), .out_13(flow_control_3_out_13), .out_14(flow_control_3_out_14),
    .out_15(flow_control_3_out_15), .out_16(flow_control_3_out_16), .out_17(flow_control_3_out_17));
endmodule

module Addr_Mux (
  input  in_1,
  input  in_2,
  input  in_3,
  input  in_4,
  input  in_5,
  input  in_6,
  input  in_7,
  input  in_8,
  input  in_9,
  input  in_10,
  input  in_11,
  input  in_12,
  input  in_13,
  input  in_14,
  input  in_15,
  output out_16,
  output out_17,
  output out_18,
  output out_19
);

  wire flow_control_1_out_10, flow_control_1_out_11, flow_control_1_out_12, flow_control_1_out_13,
       flow_control_1_out_14, flow_control_1_out_15, flow_control_1_out_16, flow_control_1_out_17,
       flow_control_2_out_10, flow_control_2_out_11, flow_control_2_out_12, flow_control_2_out_13,
       flow_control_2_out_14, flow_control_2_out_15, flow_control_2_out_16, flow_control_2_out_17,
       flow_control_3_out_10, flow_control_3_out_11, flow_control_3_out_12, flow_control_3_out_13,
       flow_control_3_out_14, flow_control_3_out_15, flow_control_3_out_16, flow_control_3_out_17,
       n3_input_1_output_1_out_29;

  Flow_Control flow_control_1 (
    .in_9(in_10), .in_1(in_6), .in_2(in_7), .in_3(in_8), .in_4(in_9), .in_5(1'b0), .in_6(1'b0), .in_7(1'b0),
    .in_8(1'b0), .out_10(flow_control_1_out_10), .out_11(flow_control_1_out_11),
    .out_12(flow_control_1_out_12), .out_13(flow_control_1_out_13), .out_14(flow_control_1_out_14),
    .out_15(flow_control_1_out_15), .out_16(flow_control_1_out_16), .out_17(flow_control_1_out_17));
  Flow_Control flow_control_2 (
    .in_9(in_5), .in_1(in_1), .in_2(in_2), .in_3(in_3), .in_4(in_4), .in_5(1'b0), .in_6(1'b0), .in_7(1'b0),
    .in_8(1'b0), .out_10(flow_control_2_out_10), .out_11(flow_control_2_out_11),
    .out_12(flow_control_2_out_12), .out_13(flow_control_2_out_13), .out_14(flow_control_2_out_14),
    .out_15(flow_control_2_out_15), .out_16(flow_control_2_out_16), .out_17(flow_control_2_out_17));
  _3_Input_1_Output u_3_input_1_output_1 (
    .in_1(flow_control_1_out_10), .in_2(flow_control_1_out_11), .in_3(flow_control_1_out_12),
    .in_4(flow_control_1_out_13), .in_5(flow_control_1_out_14), .in_6(flow_control_1_out_15),
    .in_7(flow_control_1_out_16), .in_8(flow_control_1_out_17), .in_9(flow_control_2_out_10),
    .in_10(flow_control_2_out_11), .in_11(flow_control_2_out_12), .in_12(flow_control_2_out_13),
    .in_13(flow_control_2_out_14), .in_14(flow_control_2_out_15), .in_15(flow_control_2_out_16),
    .in_16(flow_control_2_out_17), .in_17(flow_control_3_out_10), .in_18(flow_control_3_out_11),
    .in_19(flow_control_3_out_12), .in_20(flow_control_3_out_13), .in_21(flow_control_3_out_14),
    .in_22(flow_control_3_out_15), .in_23(flow_control_3_out_16), .out_25(out_16), .out_26(out_17),
    .out_27(out_18), .out_28(out_19), .out_29(n3_input_1_output_1_out_29),
    .out_30(n3_input_1_output_1_out_29), .out_31(n3_input_1_output_1_out_29), .in_24(flow_control_3_out_17),
    .out_32(n3_input_1_output_1_out_29));
  Flow_Control flow_control_3 (
    .in_9(in_15), .in_1(in_11), .in_2(in_12), .in_3(in_13), .in_4(in_14), .in_5(1'b0), .in_6(1'b0),
    .in_7(1'b0), .in_8(1'b0), .out_10(flow_control_3_out_10), .out_11(flow_control_3_out_11),
    .out_12(flow_control_3_out_12), .out_13(flow_control_3_out_13), .out_14(flow_control_3_out_14),
    .out_15(flow_control_3_out_15), .out_16(flow_control_3_out_16), .out_17(flow_control_3_out_17));
  // also tied to GND on the sheet: n3_input_1_output_1_out_29
endmodule

module Mux___2 (
  input  in_1,
  input  in_2,
  input  in_3,
  input  in_4,
  input  in_5,
  input  in_6,
  input  in_7,
  input  in_8,
  input  in_9,
  input  in_10,
  input  in_11,
  input  in_12,
  input  in_13,
  input  in_14,
  input  in_15,
  input  in_16,
  input  in_17,
  input  in_18,
  output out_19,
  output out_20,
  output out_21,
  output out_22,
  output out_23,
  output out_24,
  output out_25,
  output out_26
);

  wire flow_control_1_out_10, flow_control_1_out_11, flow_control_1_out_12, flow_control_1_out_13,
       flow_control_1_out_14, flow_control_1_out_15, flow_control_1_out_16, flow_control_1_out_17,
       flow_control_2_out_10, flow_control_2_out_11, flow_control_2_out_12, flow_control_2_out_13,
       flow_control_2_out_14, flow_control_2_out_15, flow_control_2_out_16, flow_control_2_out_17;

  Flow_Control flow_control_1 (
    .in_9(in_18), .in_1(in_10), .in_2(in_11), .in_3(in_12), .in_4(in_13), .in_5(in_14), .in_6(in_15),
    .in_7(in_16), .in_8(in_17), .out_10(flow_control_1_out_10), .out_11(flow_control_1_out_11),
    .out_12(flow_control_1_out_12), .out_13(flow_control_1_out_13), .out_14(flow_control_1_out_14),
    .out_15(flow_control_1_out_15), .out_16(flow_control_1_out_16), .out_17(flow_control_1_out_17));
  Flow_Control flow_control_2 (
    .in_9(in_9), .in_1(in_1), .in_2(in_2), .in_3(in_3), .in_4(in_4), .in_5(in_5), .in_6(in_6), .in_7(in_7),
    .in_8(in_8), .out_10(flow_control_2_out_10), .out_11(flow_control_2_out_11),
    .out_12(flow_control_2_out_12), .out_13(flow_control_2_out_13), .out_14(flow_control_2_out_14),
    .out_15(flow_control_2_out_15), .out_16(flow_control_2_out_16), .out_17(flow_control_2_out_17));
  _3_Input_1_Output u_3_input_1_output_1 (
    .in_1(flow_control_1_out_10), .in_2(flow_control_1_out_11), .in_3(flow_control_1_out_12),
    .in_4(flow_control_1_out_13), .in_5(flow_control_1_out_14), .in_6(flow_control_1_out_15),
    .in_7(flow_control_1_out_16), .in_8(flow_control_1_out_17), .in_9(flow_control_2_out_10),
    .in_10(flow_control_2_out_11), .in_11(flow_control_2_out_12), .in_12(flow_control_2_out_13),
    .in_13(flow_control_2_out_14), .in_14(flow_control_2_out_15), .in_15(flow_control_2_out_16),
    .in_16(flow_control_2_out_17), .in_17(1'b0), .in_18(1'b0), .in_19(1'b0), .in_20(1'b0), .in_21(1'b0),
    .in_22(1'b0), .in_23(1'b0), .out_25(out_19), .out_26(out_20), .out_27(out_21), .out_28(out_22),
    .out_29(out_23), .out_30(out_24), .out_31(out_25), .in_24(1'b0), .out_32(out_26));
endmodule

module D_Flip_Flop (
  input  D,
  output Q,
  output Q_prime
);

  wire not_1_out_2;

  NOT_Gate not_1 (.out_2(not_1_out_2), .in_1(D));
  nor nor_1 (Q, not_1_out_2, Q_prime);
  nor nor_2 (Q_prime, Q, D);
endmodule

// Clock
module Clock__4_Tick_Splitter (
  input  Run,
  output _1,
  output _2,
  output _3,
  output _4
);

  wire and_3_1_out_4, and_3_2_out_4, and_3_3_out_4, clock_1_out, d_ff_1_qn, d_ff_2_q, d_ff_2_qn, d_ff_3_q,
       not_1_out_2, not_2_out_2;

  Clock clock_1 (.out(clock_1_out));
  D_Flip_Flop_part d_ff_1 (.clk(clock_1_out), .D(d_ff_1_qn), .Qn(d_ff_1_qn), .reset(d_ff_3_q));  // open: Q, preset, en
  NOT_Gate not_1 (.out_2(not_1_out_2), .in_1(d_ff_1_qn));
  D_Flip_Flop_part d_ff_2 (
    .clk(d_ff_1_qn), .D(d_ff_2_qn), .Q(d_ff_2_q), .Qn(d_ff_2_qn), .reset(d_ff_3_q));  // open: preset, en
  NOT_Gate not_2 (.out_2(not_2_out_2), .in_1(d_ff_3_q));
  D_Flip_Flop_part d_ff_3 (.clk(clock_1_out), .D(d_ff_2_q), .Q(d_ff_3_q));  // open: Qn, preset, en, reset
  AND_Gate___3 and_3_1 (.in_1(d_ff_2_qn), .in_2(d_ff_3_q), .in_3(d_ff_1_qn), .out_4(and_3_1_out_4));
  AND_Gate___3 and_3_2 (.in_1(d_ff_2_qn), .in_2(not_2_out_2), .in_3(d_ff_1_qn), .out_4(and_3_2_out_4));
  AND_Gate___3 and_3_3 (.in_1(not_1_out_2), .in_2(not_2_out_2), .in_3(d_ff_2_qn), .out_4(and_3_3_out_4));
  AND_Gate and_1 (.out_3(_1), .in_1(Run), .in_2(d_ff_2_q));
  AND_Gate and_2 (.out_3(_2), .in_1(Run), .in_2(and_3_1_out_4));
  AND_Gate and_3 (.out_3(_3), .in_1(Run), .in_2(and_3_2_out_4));
  AND_Gate and_4 (.out_3(_4), .in_1(Run), .in_2(and_3_3_out_4));
endmodule

module Clock__2_Tick_s (
  output out_1
);

  wire clock_1_out, d_ff_1_qn, d_ff_2_q, d_ff_2_qn, d_ff_3_q;

  Clock clock_1 (.out(clock_1_out));
  D_Flip_Flop_part d_ff_1 (.clk(clock_1_out), .D(d_ff_1_qn), .Qn(d_ff_1_qn), .reset(d_ff_3_q));  // open: Q, preset, en
  D_Flip_Flop_part d_ff_2 (
    .clk(d_ff_1_qn), .D(d_ff_2_qn), .Q(d_ff_2_q), .Qn(d_ff_2_qn), .reset(d_ff_3_q));  // open: preset, en
  XOR_Gate xor_1 (.in_1(d_ff_2_q), .in_2(d_ff_1_qn), .out_3(out_1));
  D_Flip_Flop_part d_ff_3 (.clk(clock_1_out), .D(d_ff_2_q), .Q(d_ff_3_q));  // open: Qn, preset, en, reset
endmodule

module Auto_Clock (
  input  Halt,
  input  Run,
  output out_3,
  output out_4,
  output out_5,
  output out_6,
  output Execute_Write,
  output Fetch_Write,
  output Fetch,
  output Execute
);

  wire clock_1_out, memory_bit_1_out_3, not_1_out_2, or_1_out_3;

  OR_Gate or_1 (.out_3(or_1_out_3), .in_1(not_1_out_2), .in_2(Halt));
  NOT_Gate not_1 (.out_2(not_1_out_2), .in_1(memory_bit_1_out_3));
  Memory_Bit memory_bit_1 (.Input(Run), .out_3(memory_bit_1_out_3), .Write(or_1_out_3));
  Clock #(.highDuration(2), .lowDuration(2)) clock_1 (.out(clock_1_out));
  AND_Gate and_1 (.out_3(out_6), .in_1(clock_1_out), .in_2(out_5));
  BUFFER_Gate buffer_1 (.in_2(memory_bit_1_out_3), .out_3(Execute_Write), .in_1(out_6));
  AND_Gate and_2 (.out_3(out_4), .in_1(clock_1_out), .in_2(out_3));
  BUFFER_Gate buffer_2 (.in_2(memory_bit_1_out_3), .out_3(Fetch_Write), .in_1(out_4));
  NOT_Gate not_2 (.out_2(out_3), .in_1(out_5));
  BUFFER_Gate buffer_3 (.in_2(memory_bit_1_out_3), .out_3(Fetch), .in_1(out_3));
  Memory_Bit memory_bit_2 (.Input(out_3), .out_3(out_5), .Write(clock_1_out));
  BUFFER_Gate buffer_4 (.in_2(memory_bit_1_out_3), .out_3(Execute), .in_1(out_5));
endmodule

module Manual_Clock (
  input  Halt,
  input  Run,
  input  in_3,
  output E,
  output EW,
  output F,
  output FW,
  output out_8,
  output out_9,
  output out_10,
  output out_11
);

  wire and_1_out_3, and_3_2_out_4, d_ff_1_qn, d_ff_2_q, d_ff_2_qn, d_ff_3_q, memory_bit_1_out_3, not_1_out_2,
       not_2_out_2, not_3_out_2, not_4_out_2, not_5_out_2, not_6_out_2, not_7_out_2, or_1_out_3, or_2_out_3,
       or_3_out_3;

  D_Flip_Flop_part d_ff_1 (.clk(and_1_out_3), .D(d_ff_1_qn), .Qn(d_ff_1_qn), .reset(d_ff_3_q));  // open: Q, preset, en
  NOT_Gate not_1 (.out_2(not_1_out_2), .in_1(d_ff_1_qn));
  D_Flip_Flop_part d_ff_2 (
    .clk(d_ff_1_qn), .D(d_ff_2_qn), .Q(d_ff_2_q), .Qn(d_ff_2_qn), .reset(d_ff_3_q));  // open: preset, en
  NOT_Gate not_2 (.out_2(not_2_out_2), .in_1(d_ff_3_q));
  D_Flip_Flop_part d_ff_3 (.clk(and_1_out_3), .D(d_ff_2_q), .Q(d_ff_3_q));  // open: Qn, preset, en, reset
  AND_Gate___3 and_3_1 (.in_1(d_ff_2_qn), .in_2(d_ff_3_q), .in_3(d_ff_1_qn), .out_4(out_11));
  AND_Gate___3 and_3_2 (.in_1(d_ff_2_qn), .in_2(not_2_out_2), .in_3(d_ff_1_qn), .out_4(and_3_2_out_4));
  AND_Gate___3 and_3_3 (.in_1(not_1_out_2), .in_2(not_2_out_2), .in_3(d_ff_2_qn), .out_4(out_9));
  NOT_Gate not_3 (.out_2(not_3_out_2), .in_1(out_9));
  AND_Gate and_1 (.out_3(and_1_out_3), .in_1(in_3), .in_2(memory_bit_1_out_3));
  NOT_Gate not_4 (.out_2(not_4_out_2), .in_1(and_3_2_out_4));
  NOT_Gate not_5 (.out_2(not_5_out_2), .in_1(out_11));
  NOT_Gate not_6 (.out_2(not_6_out_2), .in_1(d_ff_2_q));
  OR_Gate or_1 (.out_3(or_1_out_3), .in_1(not_7_out_2), .in_2(Halt));
  OR_Gate or_2 (.out_3(or_2_out_3), .in_1(d_ff_2_q), .in_2(out_11));
  OR_Gate or_3 (.out_3(or_3_out_3), .in_1(and_3_2_out_4), .in_2(out_9));
  NOT_Gate not_7 (.out_2(not_7_out_2), .in_1(memory_bit_1_out_3));
  Memory_Bit memory_bit_1 (.Input(Run), .out_3(memory_bit_1_out_3), .Write(or_1_out_3));
  AND_Gate___3 and_3_4 (.in_1(not_3_out_2), .in_2(or_2_out_3), .in_3(not_4_out_2), .out_4(out_10));
  AND_Gate___3 and_3_5 (.in_1(not_5_out_2), .in_2(or_3_out_3), .in_3(not_6_out_2), .out_4(out_8));
  AND_Gate and_2 (.out_3(E), .in_1(memory_bit_1_out_3), .in_2(out_10));
  AND_Gate and_3 (.out_3(EW), .in_1(memory_bit_1_out_3), .in_2(out_11));
  AND_Gate and_4 (.out_3(F), .in_1(memory_bit_1_out_3), .in_2(out_8));
  AND_Gate and_5 (.out_3(FW), .in_1(memory_bit_1_out_3), .in_2(out_9));
endmodule

module CPU (
  input  in_1,
  input  in_2,
  input  data_input,
  input  in_4,
  input  in_5,
  input  in_6,
  input  in_7,
  input  in_8,
  input  Load,
  input  Look,
  input  Step,
  input  Clock_Input,
  input  Start,
  input  in_14,
  input  addr_input,
  input  in_16,
  input  in_17,
  output out_18,
  output out_19,
  output out_20,
  output out_21,
  output Stopped,
  output Running,
  output out_24,
  output out_25,
  output out_26,
  output out_27,
  output out_28,
  output out_29,
  output out_30,
  output out_31,
  output out_32,
  output out_33,
  output out_34,
  output out_35
);

  wire addr_mux_1_out_16, addr_mux_1_out_17, addr_mux_1_out_18, addr_mux_1_out_19, alu_1_out_26,
       alu_1_out_27, alu_1_out_28, alu_1_out_29, alu_1_out_30, alu_1_out_31, alu_1_out_32, alu_1_output_bus,
       clock_1_out, cu_new_1_add, cu_new_1_addr_mux_ir, cu_new_1_addr_mux_pc, cu_new_1_and, cu_new_1_halt,
       cu_new_1_ir_write, cu_new_1_left_shift, cu_new_1_memory_write, cu_new_1_no_shift,
       cu_new_1_pc_increment, cu_new_1_pc_load, cu_new_1_pc_write, cu_new_1_r_mux_alu, cu_new_1_r_mux_ir,
       cu_new_1_r_mux_memory, cu_new_1_r_write, cu_new_1_right_shift, cu_new_1_subtract, cu_new_1_xor,
       IR_out_10, IR_out_11, IR_out_12, IR_out_13, manual_clock_1_e, manual_clock_1_ew, manual_clock_1_f,
       manual_clock_1_fw, memory_bank_1_out_14, memory_bank_1_out_15, memory_bank_1_out_16,
       memory_bank_1_out_17, memory_bank_1_out_18, memory_bank_1_out_19, memory_bank_1_out_20,
       memory_bank_1_out_21, mux_2_1_out_19, mux_2_1_out_20, mux_2_1_out_21, mux_2_1_out_22, mux_2_1_out_23,
       mux_2_1_out_24, mux_2_1_out_25, mux_2_1_out_26, not_1_out_2, or_1_out_3, or_2_out_3, r_mux_1_out_28,
       r_mux_1_out_29, r_mux_1_out_30, r_mux_1_out_31, r_mux_1_out_32, r_mux_1_out_33, r_mux_1_out_34,
       r_mux_1_out_35, Register_out_10, Register_out_11, Register_out_12, Register_out_13, Register_out_14,
       Register_out_15, Register_out_16, Register_out_17;
  wire [3:0] IR_out_17;

  NOT_Gate not_1 (.out_2(not_1_out_2), .in_1(Load));
  Mux___2 mux_2_1 (
    .in_9(not_1_out_2), .in_18(Load), .in_10(in_1), .in_11(in_2), .in_12(data_input), .in_13(in_4),
    .in_14(in_5), .in_15(in_6), .in_16(in_7), .in_17(in_8), .in_1(Register_out_10), .in_2(Register_out_11),
    .in_3(Register_out_12), .in_4(Register_out_13), .in_5(Register_out_14), .in_6(Register_out_15),
    .in_7(Register_out_16), .in_8(Register_out_17), .out_19(mux_2_1_out_19), .out_20(mux_2_1_out_20),
    .out_21(mux_2_1_out_21), .out_22(mux_2_1_out_22), .out_23(mux_2_1_out_23), .out_24(mux_2_1_out_24),
    .out_25(mux_2_1_out_25), .out_26(mux_2_1_out_26));
  Register_8_Bit Register (
    .Write(cu_new_1_r_write), .in_1(r_mux_1_out_28), .in_2(r_mux_1_out_29), .in_3(r_mux_1_out_30),
    .in_4(r_mux_1_out_31), .in_5(r_mux_1_out_32), .in_6(r_mux_1_out_33), .in_7(r_mux_1_out_34),
    .in_8(r_mux_1_out_35), .out_10(Register_out_10), .out_11(Register_out_11), .out_12(Register_out_12),
    .out_13(Register_out_13), .out_14(Register_out_14), .out_15(Register_out_15), .out_16(Register_out_16),
    .out_17(Register_out_17));
  Register_8_Bit IR (
    .Write(cu_new_1_ir_write), .in_1(memory_bank_1_out_14), .in_2(memory_bank_1_out_15),
    .in_3(memory_bank_1_out_16), .in_4(memory_bank_1_out_17), .in_5(memory_bank_1_out_18),
    .in_6(memory_bank_1_out_19), .in_7(memory_bank_1_out_20), .in_8(memory_bank_1_out_21),
    .out_10(IR_out_10), .out_11(IR_out_11), .out_12(IR_out_12), .out_13(IR_out_13), .out_14(IR_out_17[3]),
    .out_15(IR_out_17[2]), .out_16(IR_out_17[1]), .out_17(IR_out_17[0]));
  ALU alu_1 (
    .Add(cu_new_1_add), .XOR(cu_new_1_xor), .AND(cu_new_1_and), .No_Shift(cu_new_1_no_shift),
    .Left_Shift(cu_new_1_left_shift), .Right_Shift(cu_new_1_right_shift), .Input_Bus_1(mux_2_1_out_19),
    .Input_Bus_2(memory_bank_1_out_14), .in_3(mux_2_1_out_20), .in_11(memory_bank_1_out_15),
    .in_4(mux_2_1_out_21), .in_12(memory_bank_1_out_16), .in_5(mux_2_1_out_22), .in_13(memory_bank_1_out_17),
    .in_6(mux_2_1_out_23), .in_14(memory_bank_1_out_18), .in_7(mux_2_1_out_24), .in_15(memory_bank_1_out_19),
    .in_8(mux_2_1_out_25), .in_16(memory_bank_1_out_20), .in_9(mux_2_1_out_26), .in_17(memory_bank_1_out_21),
    .Output_Bus(alu_1_output_bus), .out_26(alu_1_out_26), .out_27(alu_1_out_27), .out_28(alu_1_out_28),
    .out_29(alu_1_out_29), .out_30(alu_1_out_30), .out_31(alu_1_out_31), .out_32(alu_1_out_32),
    .in_1(IR_out_17), .Subtract(cu_new_1_subtract));
  R_Mux r_mux_1 (
    .in_9(cu_new_1_r_mux_memory), .in_18(cu_new_1_r_mux_alu), .in_27(cu_new_1_r_mux_ir),
    .in_10(alu_1_output_bus), .in_11(alu_1_out_26), .in_12(alu_1_out_27), .in_13(alu_1_out_28),
    .in_14(alu_1_out_29), .in_15(alu_1_out_30), .in_16(alu_1_out_31), .in_17(alu_1_out_32),
    .in_1(memory_bank_1_out_14), .in_2(memory_bank_1_out_15), .in_3(memory_bank_1_out_16),
    .in_4(memory_bank_1_out_17), .in_5(memory_bank_1_out_18), .in_6(memory_bank_1_out_19),
    .in_7(memory_bank_1_out_20), .in_8(memory_bank_1_out_21), .in_19(1'b0), .in_20(1'b0), .in_21(1'b0),
    .in_22(1'b0), .in_23(IR_out_17[3]), .in_24(IR_out_17[2]), .in_25(IR_out_17[1]), .in_26(IR_out_17[0]),
    .out_28(r_mux_1_out_28), .out_29(r_mux_1_out_29), .out_30(r_mux_1_out_30), .out_31(r_mux_1_out_31),
    .out_32(r_mux_1_out_32), .out_33(r_mux_1_out_33), .out_34(r_mux_1_out_34), .out_35(r_mux_1_out_35));
  NOT_Gate not_2 (.out_2(Stopped), .in_1(Running));
  // Probe on clock_1_out
  Clock clock_1 (.out(clock_1_out));
  OR_Gate___5 or_5_1 (
    .out_6(Running), .in_1(1'b0), .in_2(manual_clock_1_ew), .in_3(manual_clock_1_e),
    .in_4(manual_clock_1_fw), .in_5(manual_clock_1_f));
  CU__new cu_new_1 (
    .Execute(manual_clock_1_e), .Execute_Write(manual_clock_1_ew), .Halt(cu_new_1_halt),
    .No_Shift(cu_new_1_no_shift), .ADD(cu_new_1_add), .Left_Shift(cu_new_1_left_shift), .AND(cu_new_1_and),
    .Right_Shift(cu_new_1_right_shift), .XOR(cu_new_1_xor), .R_Write(cu_new_1_r_write),
    .R_MUX_IR(cu_new_1_r_mux_ir), .R_MUX_Memory(cu_new_1_r_mux_memory), .Memory_Write(cu_new_1_memory_write),
    .PC_Load(cu_new_1_pc_load), .PC_Increment(cu_new_1_pc_increment), .PC_Write(cu_new_1_pc_write),
    .Opcode(IR_out_10), .in_9(Register_out_10), .in_4(IR_out_11), .in_10(Register_out_11), .in_5(IR_out_12),
    .in_11(Register_out_12), .in_6(IR_out_13), .R(Register_out_13), .in_13(Register_out_14),
    .in_14(Register_out_15), .in_15(Register_out_16), .in_16(Register_out_17),
    .Addr_Mux_IR(cu_new_1_addr_mux_ir), .R_Mux_ALU(cu_new_1_r_mux_alu), .Fetch(manual_clock_1_f),
    .Fetch_Write(manual_clock_1_fw), .ADDR_Mux_PC(cu_new_1_addr_mux_pc), .IR_Write(cu_new_1_ir_write),
    .Subtract(cu_new_1_subtract));
  PC pc_1 (
    .Load(cu_new_1_pc_load), .Increment(cu_new_1_pc_increment), .Write(cu_new_1_pc_write),
    .in_2(IR_out_17[3]), .in_3(IR_out_17[2]), .in_4(IR_out_17[1]), .in_5(IR_out_17[0]), .out_9(out_32),
    .out_10(out_33), .out_11(out_34), .out_12(out_35), .Step(Step));
  Addr_Mux addr_mux_1 (
    .in_5(cu_new_1_addr_mux_pc), .in_10(cu_new_1_addr_mux_ir), .in_6(IR_out_17[3]), .in_7(IR_out_17[2]),
    .in_8(IR_out_17[1]), .in_9(IR_out_17[0]), .in_1(out_32), .in_2(out_33), .in_3(out_34), .in_4(out_35),
    .out_16(addr_mux_1_out_16), .out_17(addr_mux_1_out_17), .out_18(addr_mux_1_out_18),
    .out_19(addr_mux_1_out_19), .in_15(or_2_out_3), .in_11(in_14), .in_12(addr_input), .in_13(in_16),
    .in_14(in_17));
  OR_Gate or_1 (.out_3(or_1_out_3), .in_1(cu_new_1_memory_write), .in_2(Load));
  Manual_Clock manual_clock_1 (
    .E(manual_clock_1_e), .EW(manual_clock_1_ew), .F(manual_clock_1_f), .FW(manual_clock_1_fw),
    .in_3(Clock_Input), .Run(Start), .Halt(cu_new_1_halt), .out_8(out_18), .out_9(out_19), .out_10(out_20),
    .out_11(out_21));
  OR_Gate or_2 (.out_3(or_2_out_3), .in_1(Look), .in_2(Load));
  Memory_Bank memory_bank_1 (
    .in_1(addr_mux_1_out_16), .Address(addr_mux_1_out_17), .in_11(addr_mux_1_out_18),
    .in_12(addr_mux_1_out_19), .Write(or_1_out_3), .in_3(mux_2_1_out_19), .in_4(mux_2_1_out_20),
    .in_5(mux_2_1_out_21), .in_6(mux_2_1_out_22), .in_7(mux_2_1_out_23), .in_8(mux_2_1_out_24),
    .in_9(mux_2_1_out_25), .in_10(mux_2_1_out_26), .out_14(memory_bank_1_out_14),
    .out_15(memory_bank_1_out_15), .out_16(memory_bank_1_out_16), .out_17(memory_bank_1_out_17),
    .out_18(memory_bank_1_out_18), .out_19(memory_bank_1_out_19), .out_20(memory_bank_1_out_20),
    .out_21(memory_bank_1_out_21));
  Flow_Control flow_control_1 (
    .in_9(Look), .in_1(memory_bank_1_out_14), .in_2(memory_bank_1_out_15), .in_3(memory_bank_1_out_16),
    .in_4(memory_bank_1_out_17), .in_5(memory_bank_1_out_18), .in_6(memory_bank_1_out_19),
    .in_7(memory_bank_1_out_20), .in_8(memory_bank_1_out_21), .out_10(out_24), .out_11(out_25),
    .out_12(out_26), .out_13(out_27), .out_14(out_28), .out_15(out_29), .out_16(out_30), .out_17(out_31));

  // Notes on the sheet:
  //   step once
  //   tick twice in total before starting
  //   turn start off after the clock turns on to prevent oscillation
  //   look output
endmodule

module Interface (
  input  in_1,
  input  addr,
  input  in_3,
  input  in_4,
  input  in_5,
  input  in_6,
  input  data,
  input  in_8,
  input  in_9,
  input  in_10,
  input  in_11,
  input  in_12,
  output out_13,
  output out_14,
  output out_15,
  output out_16,
  output out_17,
  output out_18,
  output out_19,
  output out_20,
  output out_21,
  output out_22,
  output out_23,
  output out_24,
  output out_25,
  output out_26,
  output out_27,
  output out_28
);

  wire button_1_out, button_2_out, clock_1_out, Clock_Run_out, cpu_1_running, cpu_1_stopped, Step_out;

  CPU cpu_1 (
    .Stopped(cpu_1_stopped), .Running(cpu_1_running), .in_1(in_5), .in_2(in_6), .data_input(data),
    .in_4(in_8), .in_5(in_9), .in_6(in_10), .in_7(in_11), .in_8(in_12), .out_24(out_21), .out_25(out_22),
    .out_26(out_23), .out_27(out_24), .out_28(out_25), .out_29(out_26), .out_30(out_27), .out_31(out_28),
    .Look(button_1_out), .in_14(in_1), .addr_input(addr), .in_16(in_3), .in_17(in_4), .Load(button_2_out),
    .Step(Step_out), .Start(Clock_Run_out), .Clock_Input(clock_1_out), .out_32(out_17), .out_33(out_18),
    .out_34(out_19), .out_35(out_20), .out_18(out_13), .out_19(out_14), .out_20(out_15), .out_21(out_16));
  Button button_1 (.out(button_1_out));
  Button Step (.out(Step_out));
  Button button_2 (.out(button_2_out));
  LED led_1 (.in(cpu_1_running));
  LED led_2 (.in(cpu_1_stopped));
  Clock clock_1 (.out(clock_1_out));
  // Probe on clock_1_out
  Button Clock_Run (.out(Clock_Run_out));

  // Notes on the sheet:
  //   f/fw
  //   e/ew
  //   pc
  //   look
  //   load
  //   on/off
  //   output
  //   Hold to Start
endmodule
